// Logisim project 5.circ as structural Verilog: 1 circuit, main circuit main
module main (
);

  wire _4_Counter_carry, _8_Counter_carry, A_nW_out, A_q, A_qn, A_W_out, B_q, B_qn, CLK, clock_1_out, go,
       nA_nB_out, nA_W_out, not_1_out, or_1_out, or_2_out, Q, Reset_out, w;
  wire [1:0] _4_Counter_q;
  wire [3:0] _8_Counter_q;

  not not_1 (not_1_out, w);
  and nA_nB (nA_nB_out, A_qn, B_qn);
  and A_W (A_W_out, A_q, w);
  and nA_W (nA_W_out, A_qn, w);
  and A_nW (A_nW_out, A_q, not_1_out);
  or or_1 (or_1_out, nA_nB_out, A_W_out);
  or or_2 (or_2_out, nA_W_out, A_nW_out);
  T_Flip_Flop A (.clk(CLK), .T(or_1_out), .Q(A_q), .Qn(A_qn));  // open: preset, reset, en
  T_Flip_Flop B (.clk(CLK), .T(or_2_out), .Q(B_q), .Qn(B_qn));  // open: preset, reset, en
  and and_1 (Q, A_q, B_q);
  TTY #(.rows(1), .cols(33)) tty_1 (.data({6'b011000, Q}), .clk(CLK), .we(go), .clr(Reset_out));
  Counter #(.width(2), .max('h3)) _4_Counter (
    .Q(_4_Counter_q), .carry(_4_Counter_carry), .clk(CLK), .clr(Reset_out));  // open: load, D, count
  and and_2 (CLK, clock_1_out, go);
  Clock clock_1 (.out(clock_1_out));
  Counter #(.width(4), .max('h8)) _8_Counter (
    .Q(_8_Counter_q), .carry(_8_Counter_carry), .clk(_4_Counter_carry), .clr(Reset_out));  // open: load, D, count
  // Probe on _4_Counter_q
  // Probe on _8_Counter_q
  not not_2 (go, _8_Counter_carry);
  // Probe on w
  BitSelector #(.width(4)) bitselector_1 (.in(_8_Counter_q), .out(w), .sel(_4_Counter_q));
  Button Reset (.out(Reset_out));

  // Notes on the sheet:
  //   Eight gates
  //   0010100000001000101000000100001
endmodule
