// Logisim project alu.circ as structural Verilog: 1 circuit, main circuit main
module main (
);

  wire A0, A1, A2, Ad0, Ad1, Ad2, Ad3, AND_3_out, AND_4_out, AND_5_out, and_6_out, and_7_out, and_8_out, B0,
       B1, B2, C0, C1, C2, Carry1, Carry2, CIN, clock_1_out, gen0, gen1, NOT_2_out, NOT_3_out, not_4_out,
       NOT_out, OR_3_out, OR_4_out, OR_5_out, prop0, prop1, Reset_out, S0, S1, stop, xor_1_out, xor_2_out,
       xor_3_out, xor_4_out, xor_5_out, xor_6_out;
  wire [11:3] rom_1_data;

  or or_1 (prop0, A0, B0);
  or or_2 (prop1, A1, B1);
  xor xor_1 (xor_1_out, A0, B0);
  xor xor_2 (xor_2_out, A1, B1);
  xor xor_3 (xor_3_out, A2, B2);
  and and_1 (gen0, A0, B0);
  and and_2 (gen1, A1, B1);
  xor xor_4 (xor_4_out, xor_1_out, CIN);
  xor xor_5 (xor_5_out, xor_2_out, Carry1);
  xor xor_6 (xor_6_out, xor_3_out, Carry2);
  and AND_3 (AND_3_out, B0, A0);
  or OR_3 (OR_3_out, B0, A0);
  not NOT (NOT_out, A0);
  not NOT_2 (NOT_2_out, A1);
  not NOT_3 (NOT_3_out, A2);
  Multiplexer #(.select(2), .enable("false")) multiplexer_1 (
    .in0(AND_3_out), .in1(OR_3_out), .in2(NOT_out), .in3(xor_4_out), .out(C0), .sel({S1, S0}));
  and AND_4 (AND_4_out, B1, A1);
  or OR_4 (OR_4_out, B1, A1);
  and AND_5 (AND_5_out, B2, A2);
  or OR_5 (OR_5_out, B2, A2);
  // Probe on C0
  // Probe on C1
  Multiplexer #(.select(2), .enable("false")) multiplexer_2 (
    .in0(AND_4_out), .in1(OR_4_out), .in2(NOT_2_out), .in3(xor_5_out), .out(C1), .sel({S1, S0}));
  // Probe on C2
  Multiplexer #(.select(2), .enable("false")) multiplexer_3 (
    .in0(AND_5_out), .in1(OR_5_out), .in2(NOT_3_out), .in3(xor_6_out), .out(C2), .sel({S1, S0}));
  and and_6 (and_6_out, prop0, CIN);
  and and_7 (and_7_out, Carry1, prop1);
  or or_6 (Carry1, gen0, and_6_out);
  Clock clock_1 (.out(clock_1_out));
  not not_4 (not_4_out, stop);
  or or_7 (Carry2, and_7_out, gen1);
  // Probe on {C2, C1, C0}
  and and_8 (and_8_out, clock_1_out, not_4_out);
  // Probe on {S1, S0}
  // Probe on CIN
  TTY #(.rows(1), .cols(10)) tty_1 (.data({4'b0110, C2, C1, C0}), .clk(and_8_out), .clr(Reset_out));  // open: we
  Counter #(.width(4), .max('ha), .ongoal("stay")) counter_1 (
    .Q({Ad3, Ad2, Ad1, Ad0}), .carry(stop), .clk(and_8_out), .clr(Reset_out));  // open: load, D, count
  // Probe on {rom_1_data[11], CIN, S1, S0, rom_1_data[7], B2, B1, B0, rom_1_data[3], A2, A1, A0}
  ROM #(.addrWidth(4), .dataWidth(12)) rom_1 (
    .addr({Ad3, Ad2, Ad1, Ad0}),
    .data({rom_1_data[11], CIN, S1, S0, rom_1_data[7], B2, B1, B0, rom_1_data[3], A2, A1, A0}));  // open: sel
  // Probe on {B2, B1, B0}
  // Probe on {A2, A1, A0}
  Button Reset (.out(Reset_out));

  // Notes on the sheet:
  //   Cell0
  //   adds 48 to make printable
  //   5 & 3, 6 & 2, 5 | 3, 6 | 2, ~5, ~2, 7 + 7 + 0, 5 + 3 + 0, 6 + 4 + 1, 3 + 2 + 1
  //   1276256036
  //   contents of rom_1 (hex, n*v repeats v):
  //   53 62 153 162 205 202 377 353 764 723
endmodule
