// Logisim project bcd.circ as structural Verilog: 1 circuit, main circuit main
module main (
);

  wire a, and_1_out, b, c, clock_1_out, d, e, f, g, not_1_out, not_2_out, not_3_out, not_4_out, not_5_out,
       not_6_out, not_7_out, not_8_out, not_9_out, not_10_out, not_11_out, not_12_out, not_13_out,
       not_14_out, not_15_out, not_16_out, not_17_out, not_18_out, not_19_out, not_20_out, not_21_out,
       not_22_out, not_23_out, not_24_out, not_25_out, nw0_nw1_2_out, nw0_nw1_3_out, nw0_nw1_out,
       nw0_nw2_2_out, nw0_nw2_3_out, nw0_nw2_out, nw0w1_2_out, nw0w1_out, nw0w2_out, nw1w2_nw3_2_out,
       nw1w2_nw3_out, nw2w3_out, Reset_out, stop, w0, w0_nw1w2_nw3_out, w0w1_out, w0w2_out, w1, w1_nw2_2_out,
       W1_nw2_out, w2, w2_nw0_out, w3;

  not not_1 (not_1_out, w2);
  not not_2 (not_2_out, w0);
  not not_3 (not_3_out, w1);
  not not_4 (not_4_out, w0);
  not not_5 (not_5_out, w1);
  not not_6 (not_6_out, w0);
  not not_7 (not_7_out, w2);
  not not_8 (not_8_out, w2);
  not not_9 (not_9_out, w0);
  not not_10 (not_10_out, w1);
  not not_11 (not_11_out, w3);
  not not_12 (not_12_out, w2);
  not not_13 (not_13_out, w0);
  not not_14 (not_14_out, w1);
  not not_15 (not_15_out, w0);
  not not_16 (not_16_out, w2);
  not not_17 (not_17_out, w1);
  not not_18 (not_18_out, w3);
  not not_19 (not_19_out, w2);
  not not_20 (not_20_out, w0);
  not not_21 (not_21_out, w1);
  not not_22 (not_22_out, w3);
  not not_23 (not_23_out, w0);
  not not_24 (not_24_out, w2);
  and nw0_nw2 (nw0_nw2_out, not_6_out, not_7_out);
  and W1_nw2 (W1_nw2_out, w1, not_8_out);
  and nw0w1 (nw0w1_out, not_9_out, w1);
  and w0_nw1w2_nw3 (w0_nw1w2_nw3_out, w0, not_10_out, w2, not_11_out);
  and nw0_nw2_2 (nw0_nw2_2_out, not_13_out, not_12_out, not_12_out);
  and nw0w1_2 (nw0w1_2_out, not_13_out, w1);
  and w1_nw2_2 (w1_nw2_2_out, w1, not_19_out);
  and w2_nw0 (w2_nw0_out, w2, not_20_out, not_20_out);
  and nw1w2_nw3 (nw1w2_nw3_out, not_21_out, w2, not_22_out);
  and w0w1 (w0w1_out, w0, w1);
  and nw0_nw1 (nw0_nw1_out, not_2_out, not_3_out);
  and nw0_nw1_2 (nw0_nw1_2_out, not_4_out, not_5_out);
  or or_1 (e, nw0_nw2_2_out, nw0w1_2_out);
  and nw0_nw2_3 (nw0_nw2_3_out, not_23_out, not_23_out, not_24_out);
  or or_2 (b, w0w1_out, not_1_out, nw0_nw1_out);
  or or_3 (c, w0, nw0_nw1_2_out, w2);
  or or_4 (d, nw0_nw2_out, W1_nw2_out, nw0w1_out, w0_nw1w2_nw3_out, w3);
  and nw0_nw1_3 (nw0_nw1_3_out, not_15_out, not_14_out);
  and nw0w2 (nw0w2_out, not_15_out, w2);
  and nw2w3 (nw2w3_out, not_16_out, w3);
  and nw1w2_nw3_2 (nw1w2_nw3_2_out, not_17_out, w2, not_18_out);
  and w0w2 (w0w2_out, w0, w2);
  or or_5 (f, nw0_nw1_3_out, nw0w2_out, nw2w3_out, nw1w2_nw3_2_out);
  or or_6 (g, w1_nw2_2_out, w2_nw0_out, nw1w2_nw3_out, w3);
  or or_7 (a, nw0_nw2_3_out, w0w2_out, w1, w3);
  _7_Segment_Display u_7_segment_display_1 (.g(g), .f(f), .a(a), .b(b), .e(e), .d(d), .c(c));  // open: dp
  Clock clock_1 (.out(clock_1_out));
  // Probe on {w3, w2, w1, w0}
  and and_1 (and_1_out, clock_1_out, not_25_out);
  not not_25 (not_25_out, stop);
  TTY #(.rows(10), .cols(1)) tty_1 (.data({3'b100, d, c, b, a}), .clk(and_1_out), .clr(Reset_out));  // open: we
  Counter #(.width(4), .max('h9), .ongoal("stay")) counter_1 (
    .Q({w3, w2, w1, w0}), .carry(stop), .clk(and_1_out), .clr(Reset_out));  // open: load, D, count
  TTY #(.rows(10), .cols(1)) tty_2 (.data({4'b0110, g, f, e}), .clk(and_1_out), .clr(Reset_out));  // open: we
  Button Reset (.out(Reset_out));

  // Notes on the sheet:
  //   C
  //   D
  //   E
  //   F
  //   G
  //   A
  //   B
  //   O
  //   F
  //   K
  //   O
  //   F
  //   M
  //   M
  //   G
  //   O
  //   3
  //   0
  //   5
  //   4
  //   6
  //   6
  //   7
  //   0
  //   7
endmodule
