// Logisim project func.circ as structural Verilog: 1 circuit, main circuit main
module main (
);

  wire and_1_out, and_2_out, and_3_out, and_4_out, and_5_out, and_6_out, and_7_out, clock, f1, f2, go,
       not_1_out, not_2_out, not_3_out, not_4_out, not_5_out, Reset_out, t_ff_1_q, t_ff_2_q, t_ff_3_q,
       t_ff_4_q, x1, x2, x3, x4;

  not not_1 (not_1_out, x1);
  not not_2 (not_2_out, x3);
  not not_3 (not_3_out, x4);
  not not_4 (not_4_out, x1);
  and and_1 (and_1_out, not_4_out, x2);
  and and_2 (and_2_out, x2, x3);
  not not_5 (not_5_out, x4);
  and and_3 (and_3_out, not_1_out, x2, x4);
  and and_4 (and_4_out, x2, not_2_out, not_3_out);
  and and_5 (and_5_out, x2, not_5_out, not_5_out);
  and and_6 (and_6_out, x1, x2, x3);
  or or_1 (f2, and_1_out, and_2_out, and_5_out);
  and and_7 (and_7_out, not_1_out, x2, x3);
  or or_2 (f1, and_7_out, and_3_out, and_6_out, and_4_out);
  Clock clock_1 (.out(clock));
  // Probe on f1
  // Probe on {x1, x2, x3, x4}
  T_Flip_Flop t_ff_1 (.clk(clock), .T(1'b1), .Q(t_ff_1_q), .Qn(x4), .preset(Reset_out), .en(go));  // open: reset
  // Probe on f2
  T_Flip_Flop t_ff_2 (.clk(t_ff_1_q), .T(1'b1), .Q(t_ff_2_q), .Qn(x3), .preset(Reset_out));  // open: reset, en
  TTY #(.rows(1), .cols(18)) tty_1 (.data({6'b011000, f1}), .clk(clock), .we(go), .clr(Reset_out));
  T_Flip_Flop t_ff_3 (.clk(t_ff_2_q), .T(1'b1), .Q(t_ff_3_q), .Qn(x2), .preset(Reset_out));  // open: reset, en
  TTY #(.rows(1), .cols(18)) tty_2 (.data({6'b011000, f2}), .clk(clock), .we(go), .clr(Reset_out));
  T_Flip_Flop t_ff_4 (.clk(t_ff_3_q), .T(1'b1), .Q(t_ff_4_q), .Qn(x1), .preset(Reset_out));  // open: reset, en
  Button Reset (.out(Reset_out));
  T_Flip_Flop t_ff_5 (.clk(t_ff_4_q), .T(1'b1), .Q(go), .preset(Reset_out));  // open: Qn, reset, en

  // Notes on the sheet:
  //   X1
  //   X2
  //   X3
  //   X4
  //   X1
  //   X2
  //   X3
  //   X4
  //   Function #1
  //   Function #2
  //   X2X3
  //   ~X1X2X4
  //   ~X1X2
  //   ~X1X2X3
  //   X1X2X3
  //   X2~X3~X4
  //   X2~X4
  //   Press Reset button, then Ctrl-k or Ctrl-t
  //   0000111100001011
  //   0000111100001011
endmodule
