// Logisim project lab1.circ as structural Verilog: 6 circuits, main circuit Main
module Main (
);

  wire and_1_out, and_2_out, and_3_out, and_4_out, and_5_out, and_6_out, and_7_out, and_8_out, and_9_out,
       and_10_out, and_11_out, and_12_out, and_13_out, and_14_out, and_15_out, and_16_out, and_17_out,
       and_18_out, Clock, Logging, ND, not_1_out, not_2_out, not_3_out, not_4_out, not_5_out, not_6_out,
       not_7_out, not_8_out, not_9_out, not_10_out, not_11_out, not_12_out, not_13_out, not_14_out,
       not_15_out, not_16_out, not_17_out, not_18_out, not_19_out, not_20_out, not_21_out, not_22_out,
       not_23_out, not_24_out, not_25_out, not_26_out, not_27_out, not_28_out, not_29_out, not_30_out,
       not_31_out, not_32_out, not_33_out, not_34_out, not_35_out, not_36_out, not_37_out, SequentialOutput,
       X;
  wire [2:0] CombinationalOutput, ROMCombinationalOutput;
  wire [3:0] rom_2_data;
  wire [3:1] register_1_q;
  wire [7:0] Input;

  Combinational_Input combinational_input_1 (
    .In7(Input[7]), .In6(Input[6]), .In5(Input[5]), .In4(Input[4]), .In3(Input[3]), .In2(Input[2]),
    .In1(Input[1]), .In0(Input[0]), .Clock(Clock));
  Sequential_Input sequential_input_1 (.X(X), .Logging(Logging), .Clock(Clock), .Not_Done(ND));
  Clock clock_1 (.out(Clock));
  not not_1 (not_1_out, Input[4]);
  not not_2 (not_2_out, Input[3]);
  not not_3 (not_3_out, Input[2]);
  not not_4 (not_4_out, Input[4]);
  not not_5 (not_5_out, Input[1]);
  not not_6 (not_6_out, Input[4]);
  not not_7 (not_7_out, Input[0]);
  not not_8 (not_8_out, Input[4]);
  not not_9 (not_9_out, Input[1]);
  not not_10 (not_10_out, Input[4]);
  not not_11 (not_11_out, Input[5]);
  not not_12 (not_12_out, Input[4]);
  not not_13 (not_13_out, Input[7]);
  not not_14 (not_14_out, Input[3]);
  not not_15 (not_15_out, Input[2]);
  not not_16 (not_16_out, Input[7]);
  not not_17 (not_17_out, Input[2]);
  not not_18 (not_18_out, Input[7]);
  not not_19 (not_19_out, Input[1]);
  not not_20 (not_20_out, Input[0]);
  not not_21 (not_21_out, Input[7]);
  not not_22 (not_22_out, Input[7]);
  not not_23 (not_23_out, Input[7]);
  not not_24 (not_24_out, Input[4]);
  not not_25 (not_25_out, Input[2]);
  not not_26 (not_26_out, Input[0]);
  not not_27 (not_27_out, Input[7]);
  not not_28 (not_28_out, Input[4]);
  not not_29 (not_29_out, Input[2]);
  not not_30 (not_30_out, Input[7]);
  not not_31 (not_31_out, Input[4]);
  not not_32 (not_32_out, Input[3]);
  not not_33 (not_33_out, Input[1]);
  not not_34 (not_34_out, Input[7]);
  not not_35 (not_35_out, Input[4]);
  not not_36 (not_36_out, Input[2]);
  not not_37 (not_37_out, Input[7]);
  and and_1 (and_1_out, not_1_out, not_2_out, not_3_out, Input[1], Input[0]);
  and and_2 (and_2_out, not_4_out, Input[2], not_5_out);
  and and_3 (and_3_out, not_6_out, Input[2], not_7_out);
  and and_4 (and_4_out, not_8_out, Input[3], not_9_out);
  and and_5 (and_5_out, not_10_out, Input[3], Input[2]);
  and and_6 (and_6_out, Input[6], not_11_out);
  and and_7 (and_7_out, Input[7], not_12_out);
  and and_8 (and_8_out, not_13_out, not_14_out, not_15_out, Input[0]);
  and and_9 (and_9_out, not_16_out, not_17_out, Input[1]);
  and and_10 (and_10_out, not_18_out, Input[2], not_19_out, not_20_out);
  and and_11 (and_11_out, not_21_out, Input[3], Input[1]);
  and and_12 (and_12_out, not_22_out, Input[4]);
  and and_13 (and_13_out, Input[5], Input[4]);
  and and_14 (and_14_out, not_23_out, not_24_out, not_25_out, not_26_out);
  and and_15 (and_15_out, not_27_out, not_28_out, not_29_out, Input[1]);
  and and_16 (and_16_out, not_30_out, not_31_out, not_32_out, Input[2], not_33_out, Input[0]);
  and and_17 (and_17_out, not_34_out, not_35_out, Input[3], not_36_out);
  and and_18 (and_18_out, not_37_out, Input[6]);
  or or_1 (CombinationalOutput[2], and_1_out, and_2_out, and_3_out, and_4_out, and_5_out, and_6_out, and_7_out);
  or or_2 (CombinationalOutput[1], and_8_out, and_9_out, and_10_out, and_11_out, and_12_out, and_13_out);
  or or_3 (CombinationalOutput[0], and_14_out, and_15_out, and_16_out, and_17_out, Input[5], and_18_out);
  // Probe on Input
  // Probe on CombinationalOutput
  // Probe on ROMCombinationalOutput
  // Probe on Logging
  // Probe on X
  // Probe on SequentialOutput
  ROM #(.dataWidth(3)) rom_1 (.addr(Input), .data(ROMCombinationalOutput));  // open: sel
  ROM #(.addrWidth(4), .dataWidth(4)) rom_2 (.addr({register_1_q, X}), .data(rom_2_data), .sel(ND));
  Register #(.width(4)) register_1 (
    .D(rom_2_data), .Q({register_1_q, SequentialOutput}), .clk(Clock));  // open: en, clr

  // Notes on the sheet:
  //   contents of rom_1 (hex, n*v repeats v):
  //   1 2 3 7 6 5 4 0  0 5 0 3 0 4 0 6  16*2 48*0 16*7 32*0 16*4 16*0 16*5 32*0  16*4 16*0 16*3
  //   contents of rom_2 (hex, n*v repeats v):
  //   0 2 4 7 8 b d f  0 2 4 7 8 b d f
endmodule

module Combinational_Input (
  input  Clock,
  output In7,
  output In6,
  output In5,
  output In4,
  output In3,
  output In2,
  output In1,
  output In0
);

  wire [7:0] counter_1_q;

  Counter #(.ongoal("stay")) counter_1 (.count(1'b1), .Q(counter_1_q), .clk(Clock));  // open: load, D, carry, clr
  ROM rom_1 (.addr(counter_1_q), .data({In7, In6, In5, In4, In3, In2, In1, In0}));  // open: sel

  // Notes on the sheet:
  //   contents of rom_1 (hex, n*v repeats v):
  //   0 1 2 3 4 5 6 7  8 9 a b c d e f  10 11 12 13 14 15 16 17  18 19 1a 1b 1c 1d 1e 1f  20 21 22 23 24
  //   25 26 27  28 29 2a 2b 2c 2d 2e 2f  30 31 32 33 34 35 36 37  38 39 3a 3b 3c 3d 3e 3f  40 41 42 43 44
  //   45 46 47  48 49 4a 4b 4c 4d 4e 4f  50 51 52 53 54 55 56 57  58 59 5a 5b 5c 5d 5e 5f  60 61 62 63 64
  //   65 66 67  68 69 6a 6b 6c 6d 6e 6f  70 71 72 73 74 75 76 77  78 79 7a 7b 7c 7d 7e 7f  80 81 82 83 84
  //   85 86 87  88 89 8a 8b 8c 8d 8e 8f  90 91 92 93 94 95 96 97  98 99 9a 9b 9c 9d 9e 9f  a0 a1 a2 a3 a4
  //   a5 a6 a7  a8 a9 aa ab ac ad ae af  b0 b1 b2 b3 b4 b5 b6 b7  b8 b9 ba bb bc bd be bf  c0 c1 c2 c3 c4
  //   c5 c6 c7  c8 c9 ca cb cc cd ce cf  d0 d1 d2 d3 d4 d5 d6 d7  d8 d9 da db dc dd de df  e0 e1 e2 e3 e4
  //   e5 e6 e7  e8 e9 ea eb ec ed ee ef  f0 f1 f2 f3 f4 f5 f6 f7  f8 f9 fa fb fc fd fe ff
endmodule

module Sequential_Input (
  input  Clock,
  output X,
  output Not_Done,
  output Logging
);

  wire counter_1_carry, not_2_out;
  wire [7:0] counter_1_q;

  Counter #(.max('h7f), .ongoal("stay")) counter_1 (
    .count(1'b1), .Q(counter_1_q), .carry(counter_1_carry), .clk(Clock));  // open: load, D, clr
  not not_1 (Not_Done, counter_1_carry);
  not not_2 (not_2_out, Logging);
  Register #(.width(1)) register_1 (.D(not_2_out), .en(Not_Done), .Q(Logging), .clk(Clock));  // open: clr
  ROM #(.dataWidth(1)) rom_1 (.addr(counter_1_q), .data(X));  // open: sel

  // Notes on the sheet:
  //   contents of rom_1 (hex, n*v repeats v):
  //   7*0 1 0 0 1 0 0 0  1 1 0 1 0 0 0 1  0 1 0 1 1 0 0 4*1  0 0 0 1 0 0 1 1  0 1 0 1 0 4*1 0 0  1 1 0 4*1
  //   0 4*1 0 1  1 1 6*0 5*1 0 0 1 0  1 1 0 0 0 1 0 6*1  0 1 7*0 1 1 1 0 1  4*0 5*1 0 0 1 4*0 1 1
endmodule

module ROM_XOR (
  input  X,
  input  Y,
  output X_XOR_Y
);

  ROM #(.addrWidth(2), .dataWidth(1)) rom_1 (.addr({X, Y}), .data(X_XOR_Y));  // open: sel

  // Notes on the sheet:
  //   contents of rom_1 (hex, n*v repeats v):
  //   0 1 1
endmodule

module ROM_Sequential (
  input  X,
  input  Clock,
  output [1:0] Out
);

  wire [1:1] register_1_q;
  wire [2:0] rom_1_data;

  ROM #(.addrWidth(2), .dataWidth(3)) rom_1 (.addr({register_1_q[1], X}), .data(rom_1_data));  // open: sel
  Register #(.width(3)) register_1 (.D(rom_1_data), .Q({register_1_q[1], Out}), .clk(Clock));  // open: en, clr
  ROM #(.addrWidth(4), .dataWidth(4)) rom_2 ();  // open: addr, data, sel

  // Notes on the sheet:
  //   contents of rom_1 (hex, n*v repeats v):
  //   1 5 7 3
  //   contents of rom_2 (hex, n*v repeats v):
  //   0 2 4 7 8 b d f  0 2 4 7 8 b d f
endmodule

module Part1 (
  input  In7,
  input  In6,
  input  In5,
  input  In4,
  input  In3,
  input  In2,
  input  In1,
  input  In0,
  output Out2,
  output Out1,
  output Out0
);

  wire and_1_out, and_2_out, and_3_out, and_4_out, and_5_out, and_6_out, and_7_out, and_8_out, and_9_out,
       and_10_out, and_11_out, and_12_out, and_13_out, and_14_out, and_15_out, and_16_out, and_17_out,
       and_18_out, not_1_out, not_2_out, not_3_out, not_4_out, not_5_out, not_6_out, not_7_out, not_8_out,
       not_9_out, not_10_out, not_11_out, not_12_out, not_13_out, not_14_out, not_15_out, not_16_out,
       not_17_out, not_18_out, not_19_out, not_20_out, not_21_out, not_22_out, not_23_out, not_24_out,
       not_25_out, not_26_out, not_27_out, not_28_out, not_29_out, not_30_out, not_31_out, not_32_out,
       not_33_out, not_34_out, not_35_out, not_36_out, not_37_out;

  not not_1 (not_1_out, In4);
  not not_2 (not_2_out, In3);
  not not_3 (not_3_out, In2);
  not not_4 (not_4_out, In4);
  not not_5 (not_5_out, In1);
  not not_6 (not_6_out, In4);
  not not_7 (not_7_out, In0);
  not not_8 (not_8_out, In4);
  not not_9 (not_9_out, In1);
  not not_10 (not_10_out, In4);
  not not_11 (not_11_out, In5);
  not not_12 (not_12_out, In4);
  not not_13 (not_13_out, In7);
  not not_14 (not_14_out, In3);
  not not_15 (not_15_out, In2);
  not not_16 (not_16_out, In7);
  not not_17 (not_17_out, In2);
  not not_18 (not_18_out, In7);
  not not_19 (not_19_out, In1);
  not not_20 (not_20_out, In0);
  not not_21 (not_21_out, In7);
  not not_22 (not_22_out, In7);
  not not_23 (not_23_out, In7);
  not not_24 (not_24_out, In4);
  not not_25 (not_25_out, In2);
  not not_26 (not_26_out, In0);
  not not_27 (not_27_out, In7);
  not not_28 (not_28_out, In4);
  not not_29 (not_29_out, In2);
  not not_30 (not_30_out, In7);
  not not_31 (not_31_out, In4);
  not not_32 (not_32_out, In3);
  not not_33 (not_33_out, In1);
  not not_34 (not_34_out, In7);
  not not_35 (not_35_out, In4);
  not not_36 (not_36_out, In2);
  not not_37 (not_37_out, In7);
  and and_1 (and_1_out, not_1_out, not_2_out, not_3_out, In1, In0);
  and and_2 (and_2_out, not_4_out, In2, not_5_out);
  and and_3 (and_3_out, not_6_out, In2, not_7_out);
  and and_4 (and_4_out, not_8_out, In3, not_9_out);
  and and_5 (and_5_out, not_10_out, In3, In2);
  and and_6 (and_6_out, In6, not_11_out);
  and and_7 (and_7_out, In7, not_12_out);
  and and_8 (and_8_out, not_13_out, not_14_out, not_15_out, In0);
  and and_9 (and_9_out, not_16_out, not_17_out, In1);
  and and_10 (and_10_out, not_18_out, In2, not_19_out, not_20_out);
  and and_11 (and_11_out, not_21_out, In3, In1);
  and and_12 (and_12_out, not_22_out, In4);
  and and_13 (and_13_out, In5, In4);
  and and_14 (and_14_out, not_23_out, not_24_out, not_25_out, not_26_out);
  and and_15 (and_15_out, not_27_out, not_28_out, not_29_out, In1);
  and and_16 (and_16_out, not_30_out, not_31_out, not_32_out, In2, not_33_out, In0);
  and and_17 (and_17_out, not_34_out, not_35_out, In3, not_36_out);
  and and_18 (and_18_out, not_37_out, In6);
  or or_1 (Out2, and_1_out, and_2_out, and_3_out, and_4_out, and_5_out, and_6_out, and_7_out);
  or or_2 (Out1, and_8_out, and_9_out, and_10_out, and_11_out, and_12_out, and_13_out);
  or or_3 (Out0, and_14_out, and_15_out, and_16_out, and_17_out, In5, and_18_out);
endmodule
