// Logisim project Lab2.circ as structural Verilog: 9 circuits, main circuit Main
module Main (
);

  wire alu_1_zero, and_1_out, and_2_out, Clock, control_1_alusrc, control_1_branch, control_1_memtoreg,
       control_1_regdst, control_1_regwrite, jal_2_jal, jr, jrop, jump, MemRead, MemWrite, Op0, Op1, op5;
  wire [3:0] aluc_1_out0;
  wire [4:0] multiplexer_2_out, multiplexer_3_out;
  wire [7:0] alu_1_aluresult, alu_1_aluresult_2, alu_1_aluresult_3, alu_1_aluresult_4;
  wire [30:0] rom_1_data;
  wire [31:0] adder_1_out, adder_3_out, back, bit_extender_1_out, data, divider_1_out, multiplexer_4_out,
       multiplexer_5_out, multiplexer_6_out, Pc4, PC_q, ram_1_data, ramData, ReadData,
       register_file_1_rddata2, shifter_1_out;

  // Probe on nothing
  // Probe on nothing
  // Probe on nothing
  // Probe on nothing
  Register #(.width(32)) PC (.D(back), .en(1'b1), .Q(PC_q), .clk(Clock));  // open: clr
  Divider #(.width(32)) divider_1 (.a(PC_q), .b(32'h4), .out(divider_1_out));  // open: upper, rem
  Adder #(.width(32)) adder_1 (.a(PC_q), .b(32'h4), .out(adder_1_out));  // open: cin, cout
  Clock clock_1 (.out(Clock));
  Adder #(.width(32)) adder_2 (.a(PC_q), .b(32'h4), .out(Pc4));  // open: cin, cout
  ROM #(.dataWidth(32)) rom_1 (.addr(divider_1_out[7:0]), .data({op5, rom_1_data}));  // open: sel
  Multiplexer #(.width(32), .enable("false")) multiplexer_1 (.in0(ramData), .in1(adder_1_out), .out(data), .sel(jump));
  // Probe on data
  jrOp jrop_1 (
    .Op5(op5), .Op4(rom_1_data[30]), .Op3(rom_1_data[29]), .Op2(rom_1_data[28]), .Op1(rom_1_data[27]),
    .Op0(rom_1_data[26]), .OpJr(jrop));
  // Probe on rom_1_data[25:21]
  // Probe on rom_1_data[20:16]
  Jr jr_1 (
    .F5(rom_1_data[5]), .F4(rom_1_data[4]), .F3(rom_1_data[3]), .F2(rom_1_data[2]), .F1(rom_1_data[1]),
    .F0(rom_1_data[0]), .jr(jr));
  Control control_1 (
    .Op5(op5), .Op4(rom_1_data[30]), .Op3(rom_1_data[29]), .Op2(rom_1_data[28]), .Op1(rom_1_data[27]),
    .Op0(rom_1_data[26]), .RegDst(control_1_regdst), .Jump(jump), .ALUSrc(control_1_alusrc),
    .MemtoReg(control_1_memtoreg), .RegWrite(control_1_regwrite), .MemRead(MemRead), .MemWrite(MemWrite),
    .Branch(control_1_branch), .ALUOp1(Op1), .ALUOp0(Op0));
  Multiplexer #(.width(5), .enable("false")) multiplexer_2 (
    .in0(multiplexer_3_out), .in1({5{1'b1}}), .out(multiplexer_2_out), .sel(jal_2_jal));
  Multiplexer #(.width(5), .enable("false")) multiplexer_3 (
    .in0(rom_1_data[20:16]), .in1(rom_1_data[15:11]), .out(multiplexer_3_out), .sel(control_1_regdst));
  assign bit_extender_1_out = {{16{1'b0}}, rom_1_data[15:0]};  // Bit_Extender bit_extender_1
  // Probe on bit_extender_1_out
  JAL jal_2 (
    .Op5(op5), .Op4(rom_1_data[30]), .Op3(rom_1_data[29]), .Op2(rom_1_data[28]), .Op1(rom_1_data[27]),
    .Op0(rom_1_data[26]), .JAL(jal_2_jal));
  // Probe on multiplexer_2_out
  Register_File register_file_1 (
    .WrAddr(multiplexer_2_out), .WrData(data), .WrReg(control_1_regwrite), .RdAddr1(rom_1_data[25:21]),
    .RdAddr2(rom_1_data[20:16]), .RdData1(ReadData), .RdData2(register_file_1_rddata2), .Clock(Clock));
  Shifter #(.width(32)) shifter_1 (.in(bit_extender_1_out), .\dist (5'b00010), .out(shifter_1_out));
  Adder #(.width(32)) adder_3 (.a(Pc4), .b(shifter_1_out), .out(adder_3_out));  // open: cin, cout
  // Probe on ReadData
  Multiplexer #(.width(32), .enable("false")) multiplexer_4 (
    .in0(register_file_1_rddata2), .in1(bit_extender_1_out), .out(multiplexer_4_out), .sel(control_1_alusrc));
  ALUC aluc_1 (
    .OP1(Op0), .OP2(Op1), .F5(rom_1_data[5]), .F4(rom_1_data[4]), .F3(rom_1_data[3]), .F2(rom_1_data[2]),
    .F1(rom_1_data[1]), .F0(rom_1_data[0]), .out3(aluc_1_out0[3]), .out2(aluc_1_out0[2]),
    .out1(aluc_1_out0[1]), .out0(aluc_1_out0[0]));
  // Probe on multiplexer_4_out
  // Probe on aluc_1_out0
  Multiplexer #(.width(32), .enable("false")) multiplexer_5 (
    .in0(multiplexer_6_out), .in1({Pc4[31:28], rom_1_data[25:0], 2'b00}), .out(multiplexer_5_out), .sel(jump));
  Multiplexer #(.width(32), .enable("false")) multiplexer_6 (
    .in0(Pc4), .in1(adder_3_out), .out(multiplexer_6_out), .sel(and_2_out));
  ALU alu_1 (
    .ALUCtl(aluc_1_out0), .A(ReadData), .B(multiplexer_4_out),
    .ALUResult({alu_1_aluresult_4, alu_1_aluresult_3, alu_1_aluresult_2, alu_1_aluresult}),
    .Zero(alu_1_zero), .Shamt({5{1'b0}}));  // open: Overflow
  and and_1 (and_1_out, jrop, jr);
  Multiplexer #(.width(32), .enable("false")) multiplexer_7 (
    .in0(multiplexer_5_out), .in1(ReadData), .out(back), .sel(and_1_out));
  and and_2 (and_2_out, control_1_branch, alu_1_zero);
  // Probe on {alu_1_aluresult_4, alu_1_aluresult_3, alu_1_aluresult_2, alu_1_aluresult}
  // Probe on alu_1_aluresult
  // Probe on register_file_1_rddata2
  // Probe on ram_1_data
  RAM #(.dataWidth(32), .bus("separate")) ram_1 (
    .addr(alu_1_aluresult), .din(register_file_1_rddata2), .data(ram_1_data), .str(MemWrite), .sel(1'b1),
    .clk(Clock), .ld(MemRead));  // open: clr
  Multiplexer #(.width(32), .enable("false")) multiplexer_8 (
    .in0({alu_1_aluresult_4, alu_1_aluresult_3, alu_1_aluresult_2, alu_1_aluresult}), .in1(ram_1_data),
    .out(ramData), .sel(control_1_memtoreg));
  // Probe on register_file_1_rddata2

  // Notes on the sheet:
  //   contents of rom_1 (hex, n*v repeats v):
  //   20010008 34220005 3043ffff 232020 832822 223024 663826 aca40064  8ca80064 22482a c95025 a95827
  //   c00000e 201b0001 200c0001 23ff001c  11800003 1896022 8000010 201c0001 3e00008 201d0001 201e0001
endmodule

module ALU (
  input  [3:0] ALUCtl,
  input  [31:0] A,
  input  [31:0] B,
  input  [4:0] Shamt,
  output [31:0] ALUResult,
  output Zero,
  output Overflow
);

  wire comparator_1_lt, comparator_2_lt, comparator_3_eq, comparator_4_eq, or_2_out;
  wire [31:0] ADD, AND, NOR, OR, SLL, SLT, SLTU, SRL, SUB, XOR;

  // Probe on ALUCtl
  assign NOR = ~(A | B);  // NOR_Gate nor_1, 32 bits wide
  Adder #(.width(32)) adder_1 (.a(A), .b(B), .out(ADD));  // open: cin, cout
  Subtractor #(.width(32)) subtractor_1 (.a(A), .b(B), .out(SUB));  // open: bin, bout
  assign AND = A & B;  // AND_Gate and_1, 32 bits wide
  assign OR = A | B;  // OR_Gate or_1, 32 bits wide
  assign XOR = A ^ B;  // XOR_Gate xor_1, 32 bits wide
  Comparator #(.width(32)) comparator_1 (.a(A), .b(B), .lt(comparator_1_lt));  // open: gt, eq
  assign SLT = {{31{1'b0}}, comparator_1_lt};  // Bit_Extender bit_extender_1
  Shifter #(.width(32)) shifter_1 (.in(B), .\dist (Shamt), .out(SLL));
  Shifter #(.width(32), .shift("lr")) shifter_2 (.in(B), .\dist (Shamt), .out(SRL));
  Comparator #(.width(32), .mode("unsigned")) comparator_2 (.a(A), .b(B), .lt(comparator_2_lt));  // open: gt, eq
  assign SLTU = {{31{1'b0}}, comparator_2_lt};  // Bit_Extender bit_extender_2
  // Probe on ALUCtl
  Multiplexer #(.select(4), .width(32), .enable("false")) multiplexer_1 (
    .in0(AND), .in1(OR), .in2(ADD), .in3(SLT), .in4(NOR), .in5(XOR), .in6(SUB), .in14(SLL), .in15(SRL),
    .out(ALUResult), .sel(ALUCtl));  // open: in7, in8, in9, in10, in11, in12, in13
  Comparator #(.width(4)) comparator_3 (.a(4'b0000), .b(ALUCtl), .eq(comparator_3_eq));  // open: gt, lt
  Comparator #(.width(4)) comparator_4 (.a(ALUCtl), .b(4'b0001), .eq(comparator_4_eq));  // open: gt, lt
  // Probe on ALUResult
  Overflow_Unit overflow_unit_1 (
    .Add(comparator_3_eq), .Sub(comparator_4_eq), .ASign(A[31]), .BSign(B[31]), .ResultSign(ALUResult[31]),
    .Overflow(Overflow));
  or or_2 (or_2_out, ALUResult[0], ALUResult[1], ALUResult[2], ALUResult[3], ALUResult[4], ALUResult[5], ALUResult[6], ALUResult[7], ALUResult[8], ALUResult[9], ALUResult[10], ALUResult[11], ALUResult[12], ALUResult[13], ALUResult[14], ALUResult[15], ALUResult[16], ALUResult[17], ALUResult[18], ALUResult[19], ALUResult[20], ALUResult[21], ALUResult[22], ALUResult[23], ALUResult[24], ALUResult[25], ALUResult[26], ALUResult[27], ALUResult[28], ALUResult[29], ALUResult[30], ALUResult[31]);
  not not_1 (Zero, or_2_out);

  // Other names for the same wires on the sheet: ASign = A[31]; ResultSign = ALUResult[31]; BSign = B[31]

  // Notes on the sheet:
  //   ALUCtl for ADD for top port
  //   ALUCtl for SUB for second port
endmodule

module Register_File (
  input  [4:0] WrAddr,
  input  [31:0] WrData,
  input  WrReg,
  input  [4:0] RdAddr1,
  input  [4:0] RdAddr2,
  input  Clock,
  output [31:0] RdData1,
  output [31:0] RdData2
);

  wire WrReg0, WrReg1, WrReg2, WrReg3, WrReg4, WrReg5, WrReg6, WrReg7, WrReg8, WrReg9, WrReg10, WrReg11,
       WrReg12, WrReg13, WrReg14, WrReg15, WrReg16, WrReg17, WrReg18, WrReg19, WrReg20, WrReg21, WrReg22,
       WrReg23, WrReg24, WrReg25, WrReg26, WrReg27, WrReg28, WrReg29, WrReg30, WrReg31;
  wire [31:0] RegData1, RegData2, RegData3, RegData4, RegData5, RegData6, RegData7, RegData8, RegData9,
       RegData10, RegData11, RegData12, RegData13, RegData14, RegData15, RegData16, RegData17, RegData18,
       RegData19, RegData20, RegData21, RegData22, RegData23, RegData24, RegData25, RegData26, RegData27,
       RegData28, RegData29, RegData30, RegData31;

  Demultiplexer #(.select(5), .enable("false")) demultiplexer_1 (
    .out0(WrReg0), .out1(WrReg1), .out2(WrReg2), .out3(WrReg3), .out4(WrReg4), .out5(WrReg5), .out6(WrReg6),
    .out7(WrReg7), .out8(WrReg8), .out9(WrReg9), .out10(WrReg10), .out11(WrReg11), .out12(WrReg12),
    .out13(WrReg13), .out14(WrReg14), .out15(WrReg15), .out16(WrReg16), .out17(WrReg17), .out18(WrReg18),
    .out19(WrReg19), .out20(WrReg20), .out21(WrReg21), .out22(WrReg22), .out23(WrReg23), .out24(WrReg24),
    .out25(WrReg25), .out26(WrReg26), .out27(WrReg27), .out28(WrReg28), .out29(WrReg29), .out30(WrReg30),
    .out31(WrReg31), .in(WrReg), .sel(WrAddr));
  // Probe on RegData4
  Register #(.width(32)) Reg4 (.D(WrData), .en(WrReg4), .Q(RegData4), .clk(Clock));  // open: clr
  // Probe on RegData8
  Register #(.width(32)) Reg8 (.D(WrData), .en(WrReg8), .Q(RegData8), .clk(Clock));  // open: clr
  // Probe on RegData12
  Register #(.width(32)) Reg12 (.D(WrData), .en(WrReg12), .Q(RegData12), .clk(Clock));  // open: clr
  // Probe on RegData16
  Register #(.width(32)) Reg16 (.D(WrData), .en(WrReg16), .Q(RegData16), .clk(Clock));  // open: clr
  // Probe on RegData20
  Register #(.width(32)) Reg20 (.D(WrData), .en(WrReg20), .Q(RegData20), .clk(Clock));  // open: clr
  // Probe on RegData24
  Register #(.width(32)) Reg24 (.D(WrData), .en(WrReg24), .Q(RegData24), .clk(Clock));  // open: clr
  // Probe on RegData28
  Register #(.width(32)) Reg28 (.D(WrData), .en(WrReg28), .Q(RegData28), .clk(Clock));  // open: clr
  Register #(.width(32)) Reg1 (.D(WrData), .en(WrReg1), .Q(RegData1), .clk(Clock));  // open: clr
  Register #(.width(32)) Reg5 (.D(WrData), .en(WrReg5), .Q(RegData5), .clk(Clock));  // open: clr
  Register #(.width(32)) Reg9 (.D(WrData), .en(WrReg9), .Q(RegData9), .clk(Clock));  // open: clr
  Register #(.width(32)) Reg13 (.D(WrData), .en(WrReg13), .Q(RegData13), .clk(Clock));  // open: clr
  Register #(.width(32)) Reg17 (.D(WrData), .en(WrReg17), .Q(RegData17), .clk(Clock));  // open: clr
  Register #(.width(32)) Reg21 (.D(WrData), .en(WrReg21), .Q(RegData21), .clk(Clock));  // open: clr
  Register #(.width(32)) Reg25 (.D(WrData), .en(WrReg25), .Q(RegData25), .clk(Clock));  // open: clr
  Register #(.width(32)) Reg29 (.D(WrData), .en(WrReg29), .Q(RegData29), .clk(Clock));  // open: clr
  // Probe on RegData1
  // Probe on RegData5
  // Probe on RegData9
  // Probe on RegData13
  // Probe on RegData17
  // Probe on RegData21
  // Probe on RegData25
  // Probe on RegData29
  // Probe on RegData2
  Register #(.width(32)) Reg2 (.D(WrData), .en(WrReg2), .Q(RegData2), .clk(Clock));  // open: clr
  // Probe on RegData6
  Register #(.width(32)) Reg6 (.D(WrData), .en(WrReg6), .Q(RegData6), .clk(Clock));  // open: clr
  // Probe on RegData10
  Register #(.width(32)) Reg10 (.D(WrData), .en(WrReg10), .Q(RegData10), .clk(Clock));  // open: clr
  // Probe on RegData14
  Register #(.width(32)) Reg14 (.D(WrData), .en(WrReg14), .Q(RegData14), .clk(Clock));  // open: clr
  // Probe on RegData18
  Register #(.width(32)) Reg18 (.D(WrData), .en(WrReg18), .Q(RegData18), .clk(Clock));  // open: clr
  // Probe on RegData22
  Register #(.width(32)) Reg22 (.D(WrData), .en(WrReg22), .Q(RegData22), .clk(Clock));  // open: clr
  // Probe on RegData26
  Register #(.width(32)) Reg26 (.D(WrData), .en(WrReg26), .Q(RegData26), .clk(Clock));  // open: clr
  // Probe on RegData30
  Register #(.width(32)) Reg30 (.D(WrData), .en(WrReg30), .Q(RegData30), .clk(Clock));  // open: clr
  // Probe on RegData3
  Register #(.width(32)) Reg3 (.D(WrData), .en(WrReg3), .Q(RegData3), .clk(Clock));  // open: clr
  // Probe on RegData7
  Register #(.width(32)) Reg7 (.D(WrData), .en(WrReg7), .Q(RegData7), .clk(Clock));  // open: clr
  // Probe on RegData11
  Register #(.width(32)) Reg11 (.D(WrData), .en(WrReg11), .Q(RegData11), .clk(Clock));  // open: clr
  // Probe on RegData15
  Register #(.width(32)) Reg15 (.D(WrData), .en(WrReg15), .Q(RegData15), .clk(Clock));  // open: clr
  // Probe on RegData19
  Register #(.width(32)) Reg19 (.D(WrData), .en(WrReg19), .Q(RegData19), .clk(Clock));  // open: clr
  // Probe on RegData23
  Register #(.width(32)) Reg23 (.D(WrData), .en(WrReg23), .Q(RegData23), .clk(Clock));  // open: clr
  // Probe on RegData27
  Register #(.width(32)) Reg27 (.D(WrData), .en(WrReg27), .Q(RegData27), .clk(Clock));  // open: clr
  // Probe on RegData31
  Register #(.width(32)) Reg31 (.D(WrData), .en(WrReg31), .Q(RegData31), .clk(Clock));  // open: clr
  Multiplexer #(.select(5), .width(32), .enable("false")) multiplexer_1 (
    .in0({32{1'b0}}), .in1(RegData1), .in2(RegData2), .in3(RegData3), .in4(RegData4), .in5(RegData5),
    .in6(RegData6), .in7(RegData7), .in8(RegData8), .in9(RegData9), .in10(RegData10), .in11(RegData11),
    .in12(RegData12), .in13(RegData13), .in14(RegData14), .in15(RegData15), .in16(RegData16),
    .in17(RegData17), .in18(RegData18), .in19(RegData19), .in20(RegData20), .in21(RegData21),
    .in22(RegData22), .in23(RegData23), .in24(RegData24), .in25(RegData25), .in26(RegData26),
    .in27(RegData27), .in28(RegData28), .in29(RegData29), .in30(RegData30), .in31(RegData31), .out(RdData1),
    .sel(RdAddr1));
  Multiplexer #(.select(5), .width(32), .enable("false")) multiplexer_2 (
    .in0({32{1'b0}}), .in1(RegData1), .in2(RegData2), .in3(RegData3), .in4(RegData4), .in5(RegData5),
    .in6(RegData6), .in7(RegData7), .in8(RegData8), .in9(RegData9), .in10(RegData10), .in11(RegData11),
    .in12(RegData12), .in13(RegData13), .in14(RegData14), .in15(RegData15), .in16(RegData16),
    .in17(RegData17), .in18(RegData18), .in19(RegData19), .in20(RegData20), .in21(RegData21),
    .in22(RegData22), .in23(RegData23), .in24(RegData24), .in25(RegData25), .in26(RegData26),
    .in27(RegData27), .in28(RegData28), .in29(RegData29), .in30(RegData30), .in31(RegData31), .out(RdData2),
    .sel(RdAddr2));
endmodule

module Overflow_Unit (
  input  Add,
  input  Sub,
  input  ASign,
  input  BSign,
  input  ResultSign,
  output Overflow
);

  wire and_1_out, and_2_out, or_1_out, xnor_1_out, xor_1_out, xor_2_out;

  xnor xnor_1 (xnor_1_out, ASign, BSign);
  xor xor_1 (xor_1_out, ASign, BSign);
  and and_1 (and_1_out, xnor_1_out, Add);
  and and_2 (and_2_out, xor_1_out, Sub);
  or or_1 (or_1_out, and_1_out, and_2_out);
  xor xor_2 (xor_2_out, ResultSign, ASign);
  and and_3 (Overflow, or_1_out, xor_2_out);

  // Notes on the sheet:
  //   Overflow occurs when doing addition and sign(A) == sign(B) && sign(result) != sign(A)
  //   Or
  //   Overflow occurs when doing subtraction and sign(A) != sign(B) && sign(result) != sign(A)
endmodule

module ALUC (
  input  OP1,
  input  OP2,
  input  F5,
  input  F4,
  input  F3,
  input  F2,
  input  F1,
  input  F0,
  output out3,
  output out2,
  output out1,
  output out0
);

  wire and_1_out, and_2_out, and_3_out, and_4_out, and_5_out, and_6_out, and_7_out, and_8_out, and_9_out,
       and_10_out, and_11_out, and_12_out, and_13_out, and_14_out, and_15_out, and_16_out, and_17_out,
       and_18_out, and_19_out, and_20_out, and_21_out, and_22_out, and_23_out, and_24_out, and_25_out,
       and_26_out, and_27_out, and_28_out, and_29_out, not_1_out, not_2_out, not_3_out, not_4_out, not_5_out,
       not_6_out, not_7_out, not_8_out, not_9_out, not_10_out, not_11_out, not_12_out, not_13_out,
       not_14_out, not_15_out, not_16_out, not_17_out, not_18_out, not_19_out, not_20_out, not_21_out,
       not_22_out, not_23_out, not_24_out, not_25_out, not_26_out, not_27_out, not_28_out, not_29_out,
       not_30_out, not_31_out, not_32_out, not_33_out, not_34_out, not_35_out, not_36_out, not_37_out,
       not_38_out, not_39_out;

  not not_1 (not_1_out, OP1);
  not not_2 (not_2_out, F5);
  not not_3 (not_3_out, OP1);
  not not_4 (not_4_out, F2);
  not not_5 (not_5_out, F3);
  not not_6 (not_6_out, OP1);
  not not_7 (not_7_out, F1);
  not not_8 (not_8_out, OP1);
  not not_9 (not_9_out, F0);
  not not_10 (not_10_out, F5);
  not not_11 (not_11_out, F5);
  not not_12 (not_12_out, F5);
  not not_13 (not_13_out, F4);
  not not_14 (not_14_out, F3);
  not not_15 (not_15_out, F2);
  not not_16 (not_16_out, OP1);
  and and_1 (and_1_out, not_16_out, not_17_out);
  not not_17 (not_17_out, OP2);
  not not_18 (not_18_out, OP1);
  and and_2 (and_2_out, not_18_out, not_19_out);
  not not_19 (not_19_out, F5);
  not not_20 (not_20_out, F2);
  not not_21 (not_21_out, OP1);
  and and_3 (and_3_out, not_21_out, F3);
  not not_22 (not_22_out, OP1);
  and and_4 (and_4_out, not_22_out, F4);
  not not_23 (not_23_out, F4);
  not not_24 (not_24_out, F3);
  not not_25 (not_25_out, F1);
  not not_26 (not_26_out, OP1);
  not not_27 (not_27_out, F4);
  not not_28 (not_28_out, F3);
  not not_29 (not_29_out, F0);
  not not_30 (not_30_out, F4);
  not not_31 (not_31_out, F2);
  not not_32 (not_32_out, F0);
  not not_33 (not_33_out, F1);
  not not_34 (not_34_out, F4);
  not not_35 (not_35_out, F4);
  not not_36 (not_36_out, F2);
  not not_37 (not_37_out, F0);
  not not_38 (not_38_out, F5);
  not not_39 (not_39_out, F3);
  and and_5 (and_5_out, not_1_out, OP2, not_2_out);
  and and_6 (and_6_out, not_3_out, OP2, not_4_out, F0);
  and and_7 (and_7_out, OP2, not_5_out, F1);
  and and_8 (and_8_out, OP2, F1, F0);
  and and_9 (and_9_out, OP2, F2, F1);
  and and_10 (and_10_out, not_6_out, OP2, F3, not_7_out);
  and and_11 (and_11_out, not_8_out, OP2, F4);
  and and_12 (and_12_out, OP1, F1, not_9_out);
  and and_13 (and_13_out, OP1, not_10_out, F2, F1);
  and and_14 (and_14_out, OP1, not_11_out, F3, F1);
  and and_15 (and_15_out, OP1, not_12_out, F4, F1);
  and and_16 (and_16_out, OP1, F5, not_13_out, F1);
  and and_17 (and_17_out, OP1, F5, not_14_out, F1);
  and and_18 (and_18_out, OP1, F5, not_15_out, F1);
  or or_1 (out1, and_1_out, and_2_out, not_20_out, and_3_out, and_4_out);
  and and_19 (and_19_out, OP2, F5, not_23_out, not_24_out, F2, not_25_out, F0);
  and and_20 (and_20_out, not_26_out, OP2, F5, not_27_out, not_28_out, F2, F1, not_29_out);
  and and_21 (and_21_out, OP2, F5, not_30_out, F3, not_31_out, F1, not_32_out);
  and and_22 (and_22_out, OP1, not_33_out, F0);
  and and_23 (and_23_out, OP1, not_34_out, F2, F0);
  and and_24 (and_24_out, OP1, not_35_out, F3);
  and and_25 (and_25_out, OP1, F3, not_36_out);
  and and_26 (and_26_out, OP1, F3, not_37_out);
  and and_27 (and_27_out, OP1, not_38_out, F4, F0);
  and and_28 (and_28_out, OP1, F5, not_39_out, F0);
  and and_29 (and_29_out, OP1, OP2, F0);
  or or_2 (out2, and_5_out, and_6_out, and_7_out, and_8_out, and_9_out, and_10_out, and_11_out, and_12_out, and_13_out, and_14_out, and_15_out, and_16_out, and_17_out, and_18_out);
  or or_3 (out0, and_19_out, and_20_out, and_21_out, and_22_out, and_23_out, and_24_out, and_25_out, and_26_out, and_27_out, and_28_out, and_29_out);

  assign out3 = 1'b0;
endmodule

module Control (
  input  Op5,
  input  Op4,
  input  Op3,
  input  Op2,
  input  Op1,
  input  Op0,
  output RegDst,
  output Jump,
  output ALUSrc,
  output MemtoReg,
  output RegWrite,
  output MemRead,
  output MemWrite,
  output Branch,
  output ALUOp1,
  output ALUOp0
);

  wire and_1_out, and_2_out, and_3_out, and_4_out, and_5_out, and_7_out, and_8_out, and_9_out, and_10_out,
       and_11_out, and_12_out, and_13_out, and_14_out, and_15_out, and_16_out, and_17_out, and_18_out,
       and_19_out, and_20_out, and_21_out, and_22_out, and_23_out, and_24_out, and_25_out, and_26_out,
       and_27_out, and_28_out, and_29_out, and_30_out, and_31_out, and_32_out, not_1_out, not_2_out,
       not_3_out, not_4_out, not_5_out, not_6_out, not_7_out, not_8_out, not_9_out, not_10_out, not_11_out,
       not_12_out, not_13_out, not_14_out, not_15_out, not_16_out, not_17_out, not_18_out, not_19_out,
       not_20_out, not_21_out, not_22_out, not_23_out, not_24_out, not_25_out, not_26_out, not_27_out,
       not_28_out, not_29_out, not_30_out, not_31_out, not_32_out, not_33_out, not_34_out, not_35_out,
       not_36_out, not_37_out, not_38_out, not_39_out, not_40_out, not_41_out, not_42_out, not_43_out,
       not_44_out, not_45_out, not_46_out, not_47_out, not_48_out, not_49_out, not_50_out, not_51_out,
       not_52_out, not_53_out, not_54_out, not_55_out, not_56_out, not_57_out, not_58_out;

  not not_1 (not_1_out, Op5);
  not not_2 (not_2_out, Op4);
  not not_3 (not_3_out, Op3);
  not not_4 (not_4_out, Op2);
  not not_5 (not_5_out, Op3);
  not not_6 (not_6_out, Op1);
  not not_7 (not_7_out, Op2);
  not not_8 (not_8_out, Op1);
  not not_9 (not_9_out, Op1);
  not not_10 (not_10_out, Op1);
  not not_11 (not_11_out, Op5);
  not not_12 (not_12_out, Op4);
  not not_13 (not_13_out, Op3);
  not not_14 (not_14_out, Op2);
  not not_15 (not_15_out, Op5);
  not not_16 (not_16_out, Op4);
  not not_17 (not_17_out, Op0);
  not not_18 (not_18_out, Op5);
  not not_19 (not_19_out, Op4);
  not not_20 (not_20_out, Op5);
  not not_21 (not_21_out, Op4);
  not not_22 (not_22_out, Op2);
  not not_23 (not_23_out, Op1);
  not not_24 (not_24_out, Op0);
  not not_25 (not_25_out, Op3);
  not not_26 (not_26_out, Op2);
  not not_27 (not_27_out, Op5);
  not not_28 (not_28_out, Op4);
  not not_29 (not_29_out, Op1);
  not not_30 (not_30_out, Op3);
  not not_31 (not_31_out, Op2);
  not not_32 (not_32_out, Op3);
  not not_33 (not_33_out, Op2);
  not not_34 (not_34_out, Op3);
  not not_35 (not_35_out, Op3);
  not not_36 (not_36_out, Op3);
  not not_37 (not_37_out, Op2);
  not not_38 (not_38_out, Op0);
  not not_39 (not_39_out, Op5);
  not not_40 (not_40_out, Op4);
  not not_41 (not_41_out, Op3);
  not not_42 (not_42_out, Op0);
  not not_43 (not_43_out, Op3);
  not not_44 (not_44_out, Op0);
  not not_45 (not_45_out, Op5);
  not not_46 (not_46_out, Op4);
  not not_47 (not_47_out, Op3);
  not not_48 (not_48_out, Op2);
  not not_49 (not_49_out, Op5);
  not not_50 (not_50_out, Op4);
  not not_51 (not_51_out, Op1);
  not not_52 (not_52_out, Op2);
  not not_53 (not_53_out, Op1);
  not not_54 (not_54_out, Op2);
  not not_55 (not_55_out, Op1);
  not not_56 (not_56_out, Op5);
  not not_57 (not_57_out, Op4);
  not not_58 (not_58_out, Op3);
  and and_1 (and_1_out, not_1_out, not_2_out, not_3_out, not_4_out);
  and and_2 (and_2_out, not_5_out, not_6_out);
  and and_3 (and_3_out, not_7_out, not_8_out, Op0);
  and and_4 (and_4_out, Op4, not_9_out);
  and and_5 (and_5_out, Op5, not_10_out);
  and and_6 (Jump, not_11_out, not_12_out, not_13_out, not_14_out, Op1);
  and and_7 (and_7_out, not_15_out, not_16_out, Op3, not_17_out);
  and and_8 (and_8_out, not_18_out, not_19_out, Op3, Op2);
  and and_9 (and_9_out, not_20_out, not_21_out, not_22_out, not_23_out, not_24_out);
  and and_10 (and_10_out, not_25_out, not_26_out, Op0);
  and and_11 (and_11_out, not_27_out, not_28_out, Op3, Op2, not_29_out);
  and and_12 (and_12_out, Op4, not_30_out, not_31_out);
  and and_13 (and_13_out, Op5, not_32_out, not_33_out);
  and and_14 (and_14_out, not_34_out, Op2, Op1);
  and and_15 (and_15_out, Op4, not_35_out, Op1);
  and and_16 (and_16_out, Op5, not_36_out, Op1);
  and and_17 (and_17_out, Op3, not_37_out, Op0);
  and and_18 (and_18_out, Op3, Op1);
  and and_19 (and_19_out, Op3, Op2, not_38_out);
  and and_20 (and_20_out, Op4, Op3);
  and and_21 (and_21_out, Op5, Op3);
  and and_22 (and_22_out, not_39_out, not_40_out, not_41_out, Op1, not_42_out);
  and and_23 (and_23_out, not_43_out, Op2);
  and and_24 (and_24_out, Op2, not_44_out);
  and and_25 (and_25_out, Op2, Op1);
  and and_26 (and_26_out, Op4, Op2);
  and and_27 (and_27_out, Op5, Op2);
  and and_28 (and_28_out, not_45_out, not_46_out, not_47_out, not_48_out);
  and and_29 (and_29_out, not_49_out, not_50_out, Op3, not_51_out, Op0);
  and and_30 (and_30_out, Op4, not_52_out, not_53_out);
  and and_31 (and_31_out, Op5, not_54_out, not_55_out);
  and and_32 (and_32_out, not_56_out, not_57_out, not_58_out, Op1);
  or or_1 (RegDst, and_1_out, and_2_out, and_3_out, and_4_out, and_5_out);
  or or_2 (ALUSrc, Op1, and_7_out, and_8_out);
  or or_3 (RegWrite, and_9_out, and_10_out, and_11_out, and_12_out, and_13_out);
  or or_4 (MemRead, and_14_out, and_15_out, and_16_out);
  or or_5 (MemWrite, and_17_out, and_18_out, and_19_out, and_20_out, and_21_out);
  or or_6 (Branch, and_22_out, and_23_out, and_24_out, and_25_out, and_26_out, and_27_out);
  or or_7 (ALUOp1, and_28_out, and_29_out, and_30_out, and_31_out);
  or or_8 (ALUOp0, and_32_out, Op2);

  assign MemtoReg = Op1;
endmodule

module Jr (
  input  F5,
  input  F4,
  input  F3,
  input  F2,
  input  F1,
  input  F0,
  output jr
);

  wire not_1_out, not_2_out, not_3_out, not_4_out, not_5_out;

  not not_1 (not_1_out, F5);
  not not_2 (not_2_out, F4);
  not not_3 (not_3_out, F2);
  not not_4 (not_4_out, F1);
  not not_5 (not_5_out, F0);
  and and_1 (jr, not_1_out, not_2_out, F3, not_3_out, not_4_out, not_5_out);
endmodule

module jrOp (
  input  Op5,
  input  Op4,
  input  Op3,
  input  Op2,
  input  Op1,
  input  Op0,
  output OpJr
);

  wire not_1_out, not_2_out, not_3_out, not_4_out, not_5_out, not_6_out;

  not not_1 (not_1_out, Op5);
  not not_2 (not_2_out, Op4);
  not not_3 (not_3_out, Op3);
  not not_4 (not_4_out, Op2);
  not not_5 (not_5_out, Op1);
  not not_6 (not_6_out, Op0);
  and and_1 (OpJr, not_1_out, not_2_out, not_3_out, not_4_out, not_5_out, not_6_out);
endmodule

module JAL (
  input  Op5,
  input  Op4,
  input  Op3,
  input  Op2,
  input  Op1,
  input  Op0,
  output JAL
);

  wire not_1_out, not_2_out, not_3_out, not_4_out;

  not not_1 (not_1_out, Op5);
  not not_2 (not_2_out, Op4);
  not not_3 (not_3_out, Op3);
  not not_4 (not_4_out, Op2);
  and and_1 (JAL, not_1_out, not_2_out, not_3_out, not_4_out, Op1, Op0);
endmodule
