// Logisim project lab3.circ as structural Verilog: 7 circuits, main circuit Main
module Main (
);

  wire alu_1_zero, ALUA, and_1_out, and_2_out, and_3_out, Clock, IorD, IRWrite, jr, jrOp, MemRead, MemWrite,
       Op0, Op1, PCSom, PCWC, PCWrite, RegWrite;
  wire [1:0] ALUB, MemReg, PCSRs, RegDest;
  wire [3:0] ALUC, NextStatr, rom_1_data;
  wire [4:0] multiplexer_1_out;
  wire [7:0] multiplexer_2_out;
  wire [15:0] Function;
  wire [31:0] A_q, adder_1_out, alu_1_aluresult, ALUOut, BackPC, bit_extender_1_out, divider_1_out, MDR_q,
       multiplexer_3_out, multiplexer_4_out, multiplexer_6_out, PC, ram_1_data, RD, ReadData,
       register_file_1_rddata2, shifter_1_out, WData;
  wire [31:16] IR;

  // Probe on nothing
  JrOp jrop_1 (.Op5(IR[31]), .Op4(IR[30]), .Op3(IR[29]), .Op2(IR[28]), .Op1(IR[27]), .Op0(IR[26]), .OpJr(jrOp));
  // Probe on IR[31:26]
  // Probe on nothing
  // Probe on nothing
  Clock clock_1 (.out(Clock));
  JR jr_2 (
    .F5(Function[5]), .F4(Function[4]), .F3(Function[3]), .F2(Function[2]), .F1(Function[1]),
    .F0(Function[0]), .jr(jr));
  // Probe on BackPC
  Register #(.width(32)) u_PC (.D(BackPC), .en(PCSom), .Q(PC), .clk(Clock));  // open: clr
  Divider #(.width(32)) divider_1 (.a(PC), .b(32'h4), .out(divider_1_out));  // open: upper, rem
  Multiplexer #(.select(2), .width(5), .enable("false")) multiplexer_1 (
    .in0(Function[15:11]), .in1(IR[20:16]), .in2({5{1'b1}}), .out(multiplexer_1_out), .sel(RegDest));  // open: in3
  ROM #(.addrWidth(10), .dataWidth(22)) rom_1 (
    .addr({IR[31:26], NextStatr}),
    .data({PCWrite, PCWC, IorD, MemRead, MemWrite, IRWrite, MemReg, PCSRs, Op1, Op0, ALUB, ALUA, RegWrite, RegDest, rom_1_data}));  // open: sel
  Multiplexer #(.width(8), .enable("false")) multiplexer_2 (
    .in0(divider_1_out[7:0]), .in1(ALUOut[7:0]), .out(multiplexer_2_out), .sel(IorD));
  // Probe on RegDest
  // Probe on multiplexer_1_out
  Register_File register_file_1 (
    .WrAddr(multiplexer_1_out), .WrData(RD), .WrReg(RegWrite), .RdAddr1(IR[25:21]), .RdAddr2(IR[20:16]),
    .RdData1(ReadData), .RdData2(register_file_1_rddata2), .Clock(Clock));
  assign bit_extender_1_out = {{16{1'b0}}, Function};  // Bit_Extender bit_extender_1
  // Probe on multiplexer_2_out
  // Probe on register_file_1_rddata2
  Shifter #(.width(32)) shifter_1 (.in(bit_extender_1_out), .\dist (5'b00010), .out(shifter_1_out));
  RAM #(.dataWidth(32), .bus("separate")) ram_1 (
    .addr(multiplexer_2_out), .din(WData), .data(ram_1_data), .str(MemWrite), .sel(1'b1), .clk(Clock),
    .ld(MemRead));  // open: clr
  Register #(.width(32)) A (.D(ReadData), .en(1'b1), .Q(A_q), .clk(Clock));  // open: clr
  Register #(.width(32)) B (.D(register_file_1_rddata2), .en(1'b1), .Q(WData), .clk(Clock));  // open: clr
  Register #(.width(32)) u_IR (.D(ram_1_data), .en(IRWrite), .Q({IR, Function}), .clk(Clock));  // open: clr
  Register #(.width(32)) MDR (.D(ram_1_data), .en(1'b1), .Q(MDR_q), .clk(Clock));  // open: clr
  Adder #(.width(32)) adder_1 (.a(PC), .b(32'h4), .out(adder_1_out));  // open: cin, cout
  Register #(.width(5)) EX_Mem_Reg ();  // open: D, en, Q, clk, clr
  Multiplexer #(.width(32), .enable("false")) multiplexer_3 (.in0(PC), .in1(A_q), .out(multiplexer_3_out), .sel(ALUA));
  // Probe on ALUB
  Multiplexer #(.select(2), .width(32), .enable("false")) multiplexer_4 (
    .in0(WData), .in1(32'h4), .in2(bit_extender_1_out), .in3(shifter_1_out), .out(multiplexer_4_out),
    .sel(ALUB));
  // Probe on multiplexer_4_out
  // Probe on bit_extender_1_out
  // Probe on shifter_1_out
  // Probe on ALUOut
  Multiplexer #(.select(2), .width(32), .enable("false")) multiplexer_5 (
    .in0(ALUOut), .in1(MDR_q), .in2(adder_1_out), .out(RD), .sel(MemReg));  // open: in3
  // Probe on {IR, Function}
  Register #(.width(4)) ROMReg (.D(rom_1_data), .en(1'b1), .Q(NextStatr), .clk(Clock));  // open: clr
  // Probe on MemReg
  Register #(.width(2)) MEM_WB_Reg ();  // open: D, en, Q, clk, clr
  // Probe on multiplexer_3_out
  ALU alu_1 (
    .ALUCtl(ALUC), .A(multiplexer_3_out), .B(multiplexer_4_out), .ALUResult(alu_1_aluresult),
    .Zero(alu_1_zero), .Shamt(Function[10:6]));  // open: Overflow
  ALUC aluc_1 (
    .OP1(Op1), .OP2(Op0), .F5(Function[5]), .F4(Function[4]), .F3(Function[3]), .F2(Function[2]),
    .F1(Function[1]), .F0(Function[0]), .out3(ALUC[3]), .out2(ALUC[2]), .out1(ALUC[1]), .out0(ALUC[0]));
  and and_1 (and_1_out, alu_1_zero, PCWC);
  or or_1 (PCSom, and_1_out, and_2_out, PCWrite);
  Register #(.width(32)) u_ALUOut (.D(alu_1_aluresult), .en(1'b1), .Q(ALUOut), .clk(Clock));  // open: clr
  // Probe on alu_1_aluresult
  // Probe on PCSRs
  and and_2 (and_2_out, jrOp, jr);
  // Probe on ALUOut
  Multiplexer #(.select(2), .width(32), .enable("false")) multiplexer_6 (
    .in0(alu_1_aluresult), .in1(ALUOut), .in2({PC[31:28], IR[25:16], Function, 2'b00}),
    .out(multiplexer_6_out), .sel(PCSRs));  // open: in3
  // Probe on ReadData
  // Probe on multiplexer_6_out
  Multiplexer #(.width(32), .enable("false")) multiplexer_7 (
    .in0(multiplexer_6_out), .in1(ReadData), .out(BackPC), .sel(and_3_out));
  and and_3 (and_3_out, jrOp, jr);
  // Probe on nothing

  // Other names for the same wires on the sheet: Opcode[5:0] = IR[31:26]; IR[15:0] = Function;
  //   ShftPC[31:2] = {PC[31:28], IR[25:16], Function}; Shifted[27:2] = {IR[25:16], Function};
  //   SA[4:0] = Function[10:6]; RA2[4:0] = IR[20:16]; RA1[4:0] = IR[25:21]

  // Notes on the sheet:
  //   contents of rom_1 (hex, n*v repeats v):
  //   250101 306 0 112 3fddfd 0 887 40  0 101 32 5*0 250101 15*0 250101 309  7*0 202000 6*0 250101 369 7*0
  //   202000 6*0  250101 308 6*0 101480 7*0 250101 15*0 250101  15*0 250101 15*0 250101 302 287 4*0 2d0
  //   8*0 250101 15*0 250101 15*0 250101 15*0 250101  302 6c7 4*0 2d0 8*0 250101 302 a87  4*0 2d0 8*0
  //   250101 15*0 250101 15*0 250101  15*0 250101 15*0 250101 15*0 250101 15*0 250101  15*0 250101 15*0
  //   250101 15*0 250101 15*0 250101  15*0 250101 15*0 250101 15*0 250101 15*0 250101  15*0 250101 15*0
  //   250101 15*0 250101 15*0 250101  7*0 21 7*0 250101 15*0 250101 15*0 250101  302 283 c0004 4050 11*0
  //   250101 15*0 250101  15*0 250101 15*0 250101 15*0 250101 15*0 250101  15*0 250101 15*0 250101 302 285
  //   0 0  a0000 10*0 250101 15*0 250101 15*0 250101 15*0  250101 15*0 250101 15*0 250101 15*0 250101 15*0
  //   250101 15*0 250101 15*0 250101 15*0 250101 15*0  250101 15*0 250101 15*0 250101 15*0 250101 15*0
  //   250101 15*0 250101 15*0 250101 15*0 250101 15*0  250101
endmodule

module ALU (
  input  [3:0] ALUCtl,
  input  [31:0] A,
  input  [31:0] B,
  input  [4:0] Shamt,
  output [31:0] ALUResult,
  output Zero,
  output Overflow
);

  wire comparator_1_lt, comparator_2_lt, comparator_3_eq, comparator_4_eq, or_2_out;
  wire [31:0] ADD, AND, NOR, OR, SLL, SLT, SLTU, SRL, SUB, XOR;

  // Probe on A
  // Probe on ALUCtl
  // Probe on B
  assign NOR = ~(A | B);  // NOR_Gate nor_1, 32 bits wide
  Adder #(.width(32)) adder_1 (.a(A), .b(B), .out(ADD));  // open: cin, cout
  Subtractor #(.width(32)) subtractor_1 (.a(A), .b(B), .out(SUB));  // open: bin, bout
  assign AND = A & B;  // AND_Gate and_1, 32 bits wide
  assign OR = A | B;  // OR_Gate or_1, 32 bits wide
  assign XOR = A ^ B;  // XOR_Gate xor_1, 32 bits wide
  Comparator #(.width(32)) comparator_1 (.a(A), .b(B), .lt(comparator_1_lt));  // open: gt, eq
  assign SLT = {{31{1'b0}}, comparator_1_lt};  // Bit_Extender bit_extender_1
  Shifter #(.width(32)) shifter_1 (.in(B), .\dist (Shamt), .out(SLL));
  Shifter #(.width(32), .shift("lr")) shifter_2 (.in(B), .\dist (Shamt), .out(SRL));
  Comparator #(.width(32), .mode("unsigned")) comparator_2 (.a(A), .b(B), .lt(comparator_2_lt));  // open: gt, eq
  assign SLTU = {{31{1'b0}}, comparator_2_lt};  // Bit_Extender bit_extender_2
  Multiplexer #(.select(4), .width(32), .enable("false")) multiplexer_1 (
    .in0(AND), .in1(OR), .in2(ADD), .in4(NOR), .in5(XOR), .in6(SUB), .in7(SLT), .in13(A), .in14(SLL),
    .in15(SRL), .out(ALUResult), .sel(ALUCtl));  // open: in3, in8, in9, in10, in11, in12
  Comparator #(.width(4)) comparator_3 (.a(4'b0000), .b(ALUCtl), .eq(comparator_3_eq));  // open: gt, lt
  Comparator #(.width(4)) comparator_4 (.a(ALUCtl), .b(4'b0001), .eq(comparator_4_eq));  // open: gt, lt
  // Probe on ALUResult
  Overflow_Unit overflow_unit_1 (
    .Add(comparator_3_eq), .Sub(comparator_4_eq), .ASign(A[31]), .BSign(B[31]), .ResultSign(ALUResult[31]),
    .Overflow(Overflow));
  or or_2 (or_2_out, ALUResult[0], ALUResult[1], ALUResult[2], ALUResult[3], ALUResult[4], ALUResult[5], ALUResult[6], ALUResult[7], ALUResult[8], ALUResult[9], ALUResult[10], ALUResult[11], ALUResult[12], ALUResult[13], ALUResult[14], ALUResult[15], ALUResult[16], ALUResult[17], ALUResult[18], ALUResult[19], ALUResult[20], ALUResult[21], ALUResult[22], ALUResult[23], ALUResult[24], ALUResult[25], ALUResult[26], ALUResult[27], ALUResult[28], ALUResult[29], ALUResult[30], ALUResult[31]);
  not not_1 (Zero, or_2_out);

  // Other names for the same wires on the sheet: ASign = A[31]; ResultSign = ALUResult[31]; BSign = B[31]

  // Notes on the sheet:
  //   ALUCtl for ADD for top port
  //   ALUCtl for SUB for second port
endmodule

module Register_File (
  input  [4:0] WrAddr,
  input  [31:0] WrData,
  input  WrReg,
  input  [4:0] RdAddr1,
  input  [4:0] RdAddr2,
  input  Clock,
  output [31:0] RdData1,
  output [31:0] RdData2
);

  wire WrReg0, WrReg1, WrReg2, WrReg3, WrReg4, WrReg5, WrReg6, WrReg7, WrReg8, WrReg9, WrReg10, WrReg11,
       WrReg12, WrReg13, WrReg14, WrReg15, WrReg16, WrReg17, WrReg18, WrReg19, WrReg20, WrReg21, WrReg22,
       WrReg23, WrReg24, WrReg25, WrReg26, WrReg27, WrReg28, WrReg29, WrReg30, WrReg31;
  wire [31:0] RegData1, RegData2, RegData3, RegData4, RegData5, RegData6, RegData7, RegData8, RegData9,
       RegData10, RegData11, RegData12, RegData13, RegData14, RegData15, RegData16, RegData17, RegData18,
       RegData19, RegData20, RegData21, RegData22, RegData23, RegData24, RegData25, RegData26, RegData27,
       RegData28, RegData29, RegData30, RegData31;

  Demultiplexer #(.select(5), .enable("false")) demultiplexer_1 (
    .out0(WrReg0), .out1(WrReg1), .out2(WrReg2), .out3(WrReg3), .out4(WrReg4), .out5(WrReg5), .out6(WrReg6),
    .out7(WrReg7), .out8(WrReg8), .out9(WrReg9), .out10(WrReg10), .out11(WrReg11), .out12(WrReg12),
    .out13(WrReg13), .out14(WrReg14), .out15(WrReg15), .out16(WrReg16), .out17(WrReg17), .out18(WrReg18),
    .out19(WrReg19), .out20(WrReg20), .out21(WrReg21), .out22(WrReg22), .out23(WrReg23), .out24(WrReg24),
    .out25(WrReg25), .out26(WrReg26), .out27(WrReg27), .out28(WrReg28), .out29(WrReg29), .out30(WrReg30),
    .out31(WrReg31), .in(WrReg), .sel(WrAddr));
  // Probe on RegData4
  Register #(.width(32)) Reg4 (.D(WrData), .en(WrReg4), .Q(RegData4), .clk(Clock));  // open: clr
  // Probe on RegData8
  Register #(.width(32)) Reg8 (.D(WrData), .en(WrReg8), .Q(RegData8), .clk(Clock));  // open: clr
  // Probe on RegData12
  Register #(.width(32)) Reg12 (.D(WrData), .en(WrReg12), .Q(RegData12), .clk(Clock));  // open: clr
  // Probe on RegData16
  Register #(.width(32)) Reg16 (.D(WrData), .en(WrReg16), .Q(RegData16), .clk(Clock));  // open: clr
  // Probe on RegData20
  Register #(.width(32)) Reg20 (.D(WrData), .en(WrReg20), .Q(RegData20), .clk(Clock));  // open: clr
  // Probe on RegData24
  Register #(.width(32)) Reg24 (.D(WrData), .en(WrReg24), .Q(RegData24), .clk(Clock));  // open: clr
  // Probe on RegData28
  Register #(.width(32)) Reg28 (.D(WrData), .en(WrReg28), .Q(RegData28), .clk(Clock));  // open: clr
  Register #(.width(32)) Reg1 (.D(WrData), .en(WrReg1), .Q(RegData1), .clk(Clock));  // open: clr
  Register #(.width(32)) Reg5 (.D(WrData), .en(WrReg5), .Q(RegData5), .clk(Clock));  // open: clr
  Register #(.width(32)) Reg9 (.D(WrData), .en(WrReg9), .Q(RegData9), .clk(Clock));  // open: clr
  Register #(.width(32)) Reg13 (.D(WrData), .en(WrReg13), .Q(RegData13), .clk(Clock));  // open: clr
  Register #(.width(32)) Reg17 (.D(WrData), .en(WrReg17), .Q(RegData17), .clk(Clock));  // open: clr
  Register #(.width(32)) Reg21 (.D(WrData), .en(WrReg21), .Q(RegData21), .clk(Clock));  // open: clr
  Register #(.width(32)) Reg25 (.D(WrData), .en(WrReg25), .Q(RegData25), .clk(Clock));  // open: clr
  Register #(.width(32)) Reg29 (.D(WrData), .en(WrReg29), .Q(RegData29), .clk(Clock));  // open: clr
  // Probe on RegData1
  // Probe on RegData5
  // Probe on RegData9
  // Probe on RegData13
  // Probe on RegData17
  // Probe on RegData21
  // Probe on RegData25
  // Probe on RegData29
  // Probe on RegData2
  Register #(.width(32)) Reg2 (.D(WrData), .en(WrReg2), .Q(RegData2), .clk(Clock));  // open: clr
  // Probe on RegData6
  Register #(.width(32)) Reg6 (.D(WrData), .en(WrReg6), .Q(RegData6), .clk(Clock));  // open: clr
  // Probe on RegData10
  Register #(.width(32)) Reg10 (.D(WrData), .en(WrReg10), .Q(RegData10), .clk(Clock));  // open: clr
  // Probe on RegData14
  Register #(.width(32)) Reg14 (.D(WrData), .en(WrReg14), .Q(RegData14), .clk(Clock));  // open: clr
  // Probe on RegData18
  Register #(.width(32)) Reg18 (.D(WrData), .en(WrReg18), .Q(RegData18), .clk(Clock));  // open: clr
  // Probe on RegData22
  Register #(.width(32)) Reg22 (.D(WrData), .en(WrReg22), .Q(RegData22), .clk(Clock));  // open: clr
  // Probe on RegData26
  Register #(.width(32)) Reg26 (.D(WrData), .en(WrReg26), .Q(RegData26), .clk(Clock));  // open: clr
  // Probe on RegData30
  Register #(.width(32)) Reg30 (.D(WrData), .en(WrReg30), .Q(RegData30), .clk(Clock));  // open: clr
  // Probe on RegData3
  Register #(.width(32)) Reg3 (.D(WrData), .en(WrReg3), .Q(RegData3), .clk(Clock));  // open: clr
  // Probe on RegData7
  Register #(.width(32)) Reg7 (.D(WrData), .en(WrReg7), .Q(RegData7), .clk(Clock));  // open: clr
  // Probe on RegData11
  Register #(.width(32)) Reg11 (.D(WrData), .en(WrReg11), .Q(RegData11), .clk(Clock));  // open: clr
  // Probe on RegData15
  Register #(.width(32)) Reg15 (.D(WrData), .en(WrReg15), .Q(RegData15), .clk(Clock));  // open: clr
  // Probe on RegData19
  Register #(.width(32)) Reg19 (.D(WrData), .en(WrReg19), .Q(RegData19), .clk(Clock));  // open: clr
  // Probe on RegData23
  Register #(.width(32)) Reg23 (.D(WrData), .en(WrReg23), .Q(RegData23), .clk(Clock));  // open: clr
  // Probe on RegData27
  Register #(.width(32)) Reg27 (.D(WrData), .en(WrReg27), .Q(RegData27), .clk(Clock));  // open: clr
  // Probe on RegData31
  Register #(.width(32)) Reg31 (.D(WrData), .en(WrReg31), .Q(RegData31), .clk(Clock));  // open: clr
  Multiplexer #(.select(5), .width(32), .enable("false")) multiplexer_1 (
    .in0({32{1'b0}}), .in1(RegData1), .in2(RegData2), .in3(RegData3), .in4(RegData4), .in5(RegData5),
    .in6(RegData6), .in7(RegData7), .in8(RegData8), .in9(RegData9), .in10(RegData10), .in11(RegData11),
    .in12(RegData12), .in13(RegData13), .in14(RegData14), .in15(RegData15), .in16(RegData16),
    .in17(RegData17), .in18(RegData18), .in19(RegData19), .in20(RegData20), .in21(RegData21),
    .in22(RegData22), .in23(RegData23), .in24(RegData24), .in25(RegData25), .in26(RegData26),
    .in27(RegData27), .in28(RegData28), .in29(RegData29), .in30(RegData30), .in31(RegData31), .out(RdData1),
    .sel(RdAddr1));
  Multiplexer #(.select(5), .width(32), .enable("false")) multiplexer_2 (
    .in0({32{1'b0}}), .in1(RegData1), .in2(RegData2), .in3(RegData3), .in4(RegData4), .in5(RegData5),
    .in6(RegData6), .in7(RegData7), .in8(RegData8), .in9(RegData9), .in10(RegData10), .in11(RegData11),
    .in12(RegData12), .in13(RegData13), .in14(RegData14), .in15(RegData15), .in16(RegData16),
    .in17(RegData17), .in18(RegData18), .in19(RegData19), .in20(RegData20), .in21(RegData21),
    .in22(RegData22), .in23(RegData23), .in24(RegData24), .in25(RegData25), .in26(RegData26),
    .in27(RegData27), .in28(RegData28), .in29(RegData29), .in30(RegData30), .in31(RegData31), .out(RdData2),
    .sel(RdAddr2));
  // Probe on RdAddr2
endmodule

module Overflow_Unit (
  input  Add,
  input  Sub,
  input  ASign,
  input  BSign,
  input  ResultSign,
  output Overflow
);

  wire and_1_out, and_2_out, or_1_out, xnor_1_out, xor_1_out, xor_2_out;

  xnor xnor_1 (xnor_1_out, ASign, BSign);
  xor xor_1 (xor_1_out, ASign, BSign);
  and and_1 (and_1_out, xnor_1_out, Add);
  and and_2 (and_2_out, xor_1_out, Sub);
  or or_1 (or_1_out, and_1_out, and_2_out);
  xor xor_2 (xor_2_out, ResultSign, ASign);
  and and_3 (Overflow, or_1_out, xor_2_out);

  // Notes on the sheet:
  //   Overflow occurs when doing addition and sign(A) == sign(B) && sign(result) != sign(A)
  //   Or
  //   Overflow occurs when doing subtraction and sign(A) != sign(B) && sign(result) != sign(A)
endmodule

module ALUC (
  input  OP1,
  input  OP2,
  input  F5,
  input  F4,
  input  F3,
  input  F2,
  input  F1,
  input  F0,
  output out3,
  output out2,
  output out1,
  output out0
);

  wire and_1_out, and_2_out, and_3_out, and_4_out, and_5_out, and_6_out, and_7_out, and_8_out, and_9_out,
       and_10_out, and_11_out, and_12_out, and_13_out, and_14_out, and_15_out, and_16_out, and_17_out,
       and_18_out, and_19_out, and_20_out, and_21_out, and_22_out, and_23_out, and_24_out, and_25_out,
       and_26_out, and_27_out, and_28_out, and_29_out, and_30_out, and_31_out, and_32_out, and_33_out,
       and_34_out, and_35_out, and_36_out, and_37_out, and_38_out, and_39_out, and_40_out, and_41_out,
       and_42_out, and_43_out, and_44_out, and_45_out, and_46_out, and_47_out, and_48_out, and_49_out,
       not_1_out, not_2_out, not_3_out, not_4_out, not_5_out, not_6_out, not_7_out, not_8_out, not_9_out,
       not_10_out, not_11_out, not_12_out, not_13_out, not_14_out, not_15_out, not_16_out, not_17_out,
       not_18_out, not_19_out, not_20_out, not_21_out, not_22_out, not_23_out, not_24_out, not_25_out,
       not_26_out, not_27_out, not_28_out, not_29_out, not_30_out, not_31_out, not_32_out, not_33_out,
       not_34_out, not_35_out, not_36_out, not_37_out, not_38_out, not_39_out, not_40_out, not_41_out,
       not_42_out, not_43_out, not_44_out, not_45_out, not_46_out, not_47_out, not_48_out, not_49_out,
       not_50_out, not_51_out, not_52_out, not_53_out, not_54_out, not_55_out, not_56_out, not_57_out,
       not_58_out, not_59_out, not_60_out, not_61_out, not_62_out, not_63_out, not_64_out, not_65_out,
       not_66_out, not_67_out, not_68_out, not_69_out, not_70_out, not_71_out, not_72_out, not_73_out,
       not_74_out, not_75_out, not_76_out, not_77_out, not_78_out, not_79_out, not_80_out, not_81_out,
       not_82_out, not_83_out, not_84_out, not_85_out, not_86_out, not_87_out, not_88_out, not_89_out,
       not_90_out, not_91_out, not_92_out, not_93_out, not_94_out, not_95_out, not_96_out, not_97_out,
       not_98_out, not_99_out, not_100_out, not_101_out, not_102_out, not_103_out, not_104_out;

  not not_1 (not_1_out, OP2);
  not not_2 (not_2_out, F5);
  not not_3 (not_3_out, F4);
  not not_4 (not_4_out, F3);
  not not_5 (not_5_out, F2);
  not not_6 (not_6_out, F0);
  not not_7 (not_7_out, OP2);
  not not_8 (not_8_out, F5);
  not not_9 (not_9_out, F4);
  not not_10 (not_10_out, F2);
  not not_11 (not_11_out, F1);
  not not_12 (not_12_out, F0);
  not not_13 (not_13_out, OP2);
  not not_14 (not_14_out, F5);
  not not_15 (not_15_out, F3);
  not not_16 (not_16_out, F2);
  not not_17 (not_17_out, F1);
  not not_18 (not_18_out, F0);
  not not_19 (not_19_out, OP1);
  not not_20 (not_20_out, F5);
  not not_21 (not_21_out, OP1);
  not not_22 (not_22_out, F2);
  not not_23 (not_23_out, F3);
  not not_24 (not_24_out, F4);
  not not_25 (not_25_out, OP1);
  not not_26 (not_26_out, F1);
  not not_27 (not_27_out, OP1);
  not not_28 (not_28_out, F3);
  not not_29 (not_29_out, OP1);
  not not_30 (not_30_out, F0);
  not not_31 (not_31_out, OP2);
  not not_32 (not_32_out, F5);
  not not_33 (not_33_out, F4);
  not not_34 (not_34_out, F2);
  not not_35 (not_35_out, F0);
  not not_36 (not_36_out, OP2);
  not not_37 (not_37_out, F5);
  not not_38 (not_38_out, F3);
  not not_39 (not_39_out, F2);
  not not_40 (not_40_out, F0);
  not not_41 (not_41_out, F0);
  not not_42 (not_42_out, F5);
  not not_43 (not_43_out, F5);
  not not_44 (not_44_out, F5);
  not not_45 (not_45_out, F4);
  not not_46 (not_46_out, F3);
  not not_47 (not_47_out, F2);
  not not_48 (not_48_out, OP1);
  not not_49 (not_49_out, OP2);
  not not_50 (not_50_out, F0);
  not not_51 (not_51_out, F3);
  not not_52 (not_52_out, F2);
  not not_53 (not_53_out, F2);
  not not_54 (not_54_out, OP1);
  not not_55 (not_55_out, F5);
  not not_56 (not_56_out, F2);
  not not_57 (not_57_out, OP1);
  not not_58 (not_58_out, F4);
  not not_59 (not_59_out, OP1);
  not not_60 (not_60_out, F1);
  not not_61 (not_61_out, OP1);
  not not_62 (not_62_out, F0);
  not not_63 (not_63_out, OP1);
  not not_64 (not_64_out, F3);
  not not_65 (not_65_out, F2);
  not not_66 (not_66_out, OP1);
  not not_67 (not_67_out, OP2);
  not not_68 (not_68_out, F4);
  not not_69 (not_69_out, F2);
  not not_70 (not_70_out, OP1);
  not not_71 (not_71_out, F5);
  not not_72 (not_72_out, F2);
  not not_73 (not_73_out, OP2);
  not not_74 (not_74_out, F5);
  not not_75 (not_75_out, F4);
  not not_76 (not_76_out, F3);
  not not_77 (not_77_out, F1);
  not not_78 (not_78_out, OP1);
  not not_79 (not_79_out, OP2);
  not not_80 (not_80_out, F4);
  not not_81 (not_81_out, F3);
  not not_82 (not_82_out, F1);
  not not_83 (not_83_out, OP1);
  not not_84 (not_84_out, F4);
  not not_85 (not_85_out, F3);
  not not_86 (not_86_out, F0);
  not not_87 (not_87_out, F4);
  not not_88 (not_88_out, F2);
  not not_89 (not_89_out, F0);
  not not_90 (not_90_out, F1);
  not not_91 (not_91_out, OP2);
  not not_92 (not_92_out, F5);
  not not_93 (not_93_out, F4);
  not not_94 (not_94_out, F2);
  not not_95 (not_95_out, F0);
  not not_96 (not_96_out, F5);
  not not_97 (not_97_out, F4);
  not not_98 (not_98_out, F2);
  not not_99 (not_99_out, F0);
  not not_100 (not_100_out, F3);
  not not_101 (not_101_out, F2);
  not not_102 (not_102_out, OP2);
  not not_103 (not_103_out, F4);
  not not_104 (not_104_out, F0);
  and and_1 (and_1_out, OP1, not_1_out, not_2_out, not_3_out, not_4_out, not_5_out, not_6_out);
  and and_2 (and_2_out, OP1, not_7_out, not_8_out, not_9_out, not_10_out, not_11_out, not_12_out);
  and and_3 (and_3_out, OP1, not_13_out, not_14_out, not_15_out, not_16_out, not_17_out, not_18_out);
  and and_4 (and_4_out, not_19_out, OP2, not_20_out);
  and and_5 (and_5_out, not_21_out, OP2, not_22_out, F0);
  and and_6 (and_6_out, OP2, not_23_out, F1);
  and and_7 (and_7_out, OP2, not_24_out, F2, F1);
  and and_8 (and_8_out, not_25_out, OP2, F3, not_26_out);
  and and_9 (and_9_out, not_27_out, OP2, F4, not_28_out);
  and and_10 (and_10_out, not_29_out, OP2, F4, not_30_out);
  and and_11 (and_11_out, OP1, not_31_out, not_32_out, not_33_out, not_34_out, not_35_out);
  and and_12 (and_12_out, OP1, not_36_out, not_37_out, not_38_out, not_39_out, not_40_out);
  and and_13 (and_13_out, OP1, F1, not_41_out);
  and and_14 (and_14_out, OP1, not_42_out, F2, F1);
  and and_15 (and_15_out, OP1, not_43_out, F3, F1);
  and and_16 (and_16_out, OP1, not_44_out, F4, F1);
  and and_17 (and_17_out, OP1, F5, not_45_out, F1);
  and and_18 (and_18_out, OP1, F5, not_46_out, F1);
  and and_19 (and_19_out, OP1, F5, not_47_out, F1);
  and and_20 (and_20_out, OP1, OP2, F1);
  and and_21 (and_21_out, not_48_out, not_49_out, not_50_out);
  and and_22 (and_22_out, not_51_out, not_52_out);
  and and_23 (and_23_out, not_53_out, F0);
  and and_24 (and_24_out, not_54_out, not_55_out, F1);
  and and_25 (and_25_out, not_56_out, F1);
  and and_26 (and_26_out, not_57_out, not_58_out, F3);
  and and_27 (and_27_out, not_59_out, F3, not_60_out);
  and and_28 (and_28_out, not_61_out, F3, not_62_out);
  and and_29 (and_29_out, not_63_out, F4, not_64_out);
  and and_30 (and_30_out, F4, not_65_out);
  and and_31 (and_31_out, not_66_out, not_67_out, F5, not_68_out);
  and and_32 (and_32_out, F5, not_69_out);
  and and_33 (and_33_out, not_70_out, OP2, not_71_out);
  and and_34 (and_34_out, OP2, not_72_out);
  and and_35 (and_35_out, not_73_out, not_74_out, not_75_out, not_76_out, F2, not_77_out, F0);
  and and_36 (and_36_out, not_78_out, not_79_out, F5, F4, F3, F2, F1, F0);
  and and_37 (and_37_out, OP2, F5, not_80_out, not_81_out, F2, not_82_out, F0);
  and and_38 (and_38_out, not_83_out, OP2, F5, not_84_out, not_85_out, F2, F1, not_86_out);
  and and_39 (and_39_out, OP2, F5, not_87_out, F3, not_88_out, F1, not_89_out);
  and and_40 (and_40_out, OP1, not_90_out, F0);
  and and_41 (and_41_out, OP1, not_91_out, not_92_out, not_93_out, not_94_out, F1, not_95_out);
  and and_42 (and_42_out, OP1, not_96_out, F2, F0);
  and and_43 (and_43_out, OP1, not_97_out, F3);
  and and_44 (and_44_out, OP1, F3, not_98_out);
  and and_45 (and_45_out, OP1, F3, not_99_out);
  and and_46 (and_46_out, OP1, F4, not_100_out, F0);
  and and_47 (and_47_out, OP1, F5, not_101_out, F0);
  and and_48 (and_48_out, OP1, not_102_out, F5, not_103_out, F2, F1, not_104_out);
  and and_49 (and_49_out, OP1, OP2, F0);
  or or_1 (out3, and_1_out, and_2_out, and_3_out);
  or or_2 (out2, and_4_out, and_5_out, and_6_out, and_7_out, and_8_out, and_9_out, and_10_out, and_11_out, and_12_out, and_13_out, and_14_out, and_15_out, and_16_out, and_17_out, and_18_out, and_19_out, and_20_out);
  or or_3 (out1, and_21_out, and_22_out, and_23_out, and_24_out, and_25_out, and_26_out, and_27_out, and_28_out, and_29_out, and_30_out, and_31_out, and_32_out, and_33_out, and_34_out);
  or or_4 (out0, and_35_out, and_36_out, and_37_out, and_38_out, and_39_out, and_40_out, and_41_out, and_42_out, and_43_out, and_44_out, and_45_out, and_46_out, and_47_out, and_48_out, and_49_out);
endmodule

module JR (
  input  F5,
  input  F4,
  input  F3,
  input  F2,
  input  F1,
  input  F0,
  output jr
);

  wire not_1_out, not_2_out, not_3_out, not_4_out, not_5_out;

  not not_1 (not_1_out, F5);
  not not_2 (not_2_out, F4);
  not not_3 (not_3_out, F2);
  not not_4 (not_4_out, F1);
  not not_5 (not_5_out, F0);
  and and_1 (jr, not_1_out, not_2_out, F3, not_3_out, not_4_out, not_5_out);
endmodule

module JrOp (
  input  Op5,
  input  Op4,
  input  Op3,
  input  Op2,
  input  Op1,
  input  Op0,
  output OpJr
);

  wire not_1_out, not_2_out, not_3_out, not_4_out, not_5_out, not_6_out;

  not not_1 (not_1_out, Op5);
  not not_2 (not_2_out, Op4);
  not not_3 (not_3_out, Op3);
  not not_4 (not_4_out, Op2);
  not not_5 (not_5_out, Op1);
  not not_6 (not_6_out, Op0);
  and and_1 (OpJr, not_1_out, not_2_out, not_3_out, not_4_out, not_5_out, not_6_out);
endmodule
