// Logisim project lab4.circ as structural Verilog: 11 circuits, main circuit Main
module Main (
);

  wire alu_1_zero, ALUOp0, ALUOp1, ALUSrc, Branch, Clock, EX_Mem_Jump, EX_Mem_RegWrite, EX_Mem_Zero_q,
       FRomBranch, ID_EX_JAL_q, ID_EX_JrOp_F_q, ID_EX_JrOp_q, ID_EX_Jump_q, ID_EX_MemRead, IF_ID_Write, JAL,
       jal_2_jal, Jl, JR_2_out, JR_3_out, Jr_F, jrfunct_1_jr, JrOp, jrop_1_opjr, Jump, Mem_WB_Jump, MemRead,
       MemToReg, MemWrite, NOP, NOP_Decode, or_1_out, PC_Write, RegDst, RegWrite;
  wire [1:0] ForA, ForB;
  wire [3:0] ALUC;
  wire [4:0] _15_11, _20_16, EX_Mem_Inst, ID_EX_15_11, ID_EX_20_16, Mem_WB_Inst, multiplexer_2_out,
       multiplexer_3_out, multiplexer_4_out, RD1_2, SA;
  wire [5:0] Funct, ID_EXFunct_q;
  wire [7:1] ID_EX_Control_q;
  wire [9:0] control_1_regdst, EX_Mem_Control_q, multiplexer_1_out;
  wire [27:0] PC4;
  wire [31:0] adder_2_out, adder_3_out, alu_1_aluresult, ALURE, bit_extender_1_out, Data, divider_1_out,
       EX_Mem_Inst_2_q, EX_Mem_PC_q, EX_MemRD2_q, FRom_PC, ID_EX_Inst_q, ID_EX_JumpADD_q, ID_EXRD1_q,
       ID_EXRD2_q, IF_ID_PC_q, JumpADD2, Mem_WB_ALUR_q, MEM_WB_Inst_2_q, Mem_WB_RD_q, multiplexer_5_out,
       multiplexer_6_out, multiplexer_7_out, multiplexer_8_out, multiplexer_9_out, multiplexer_10_out,
       PC_Back, PCAdd1, ram_1_data, RamData, ReadData, register_file_1_rddata1, register_file_1_rddata2,
       rom_1_data, SE, shifter_1_out, subtractor_1_out;
  wire [31:6] INST;
  wire [31:28] JumpADD;

  Clock clock_1 (.out(Clock));
  // Probe on INST[31:26]
  Register #(.width(5)) ID_EX_SA (.D(INST[10:6]), .en(1'b1), .Q(SA), .clk(Clock));  // open: clr
  Register #(.width(5)) ID_EX_RS (.D(INST[25:21]), .en(1'b1), .Q(RD1_2), .clk(Clock));  // open: clr
  Register #(.width(32)) PC (.D(PC_Back), .en(PC_Write), .Q(FRom_PC), .clk(Clock));  // open: clr
  Control control_1 (
    .Op5(INST[31]), .Op4(INST[30]), .Op3(INST[29]), .Op2(INST[28]), .Op1(INST[27]), .Op0(INST[26]),
    .RegDst(control_1_regdst[0]), .Jump(Jump), .ALUSrc(control_1_regdst[2]), .MemtoReg(control_1_regdst[3]),
    .RegWrite(control_1_regdst[4]), .MemRead(control_1_regdst[5]), .MemWrite(control_1_regdst[6]),
    .Branch(control_1_regdst[7]), .ALUOp1(control_1_regdst[8]), .ALUOp0(control_1_regdst[9]));
  Adder #(.width(32)) adder_1 (.a(FRom_PC), .b(32'h4), .out(PCAdd1));  // open: cin, cout
  Divider #(.width(32)) divider_1 (.a(FRom_PC), .b(32'h4), .out(divider_1_out));  // open: upper, rem
  assign bit_extender_1_out = {{16{1'b0}}, {_15_11, INST[10:6], Funct}};  // Bit_Extender bit_extender_1
  Register #(.width(6)) ID_EXFunct (.D(Funct), .en(1'b1), .Q(ID_EXFunct_q), .clk(Clock));  // open: clr
  Register #(.width(5)) ID_EX20_16 (.D(_20_16), .en(1'b1), .Q(ID_EX_20_16), .clk(Clock));  // open: clr
  Register #(.width(5)) ID_EX15_11 (.D(_15_11), .en(1'b1), .Q(ID_EX_15_11), .clk(Clock));  // open: clr
  Register #(.width(32)) IF_ID_PC (.D(PCAdd1), .en(1'b1), .Q(IF_ID_PC_q), .clk(Clock));  // open: clr
  Multiplexer #(.width(10), .enable("false")) multiplexer_1 (
    .in0({control_1_regdst[9:2], Jump, control_1_regdst[0]}), .in1({10{1'b0}}), .out(multiplexer_1_out),
    .sel(NOP));
  // Probe on multiplexer_2_out
  Multiplexer #(.width(5), .enable("false")) multiplexer_2 (
    .in0(Mem_WB_Inst), .in1({5{1'b1}}), .out(multiplexer_2_out), .sel(JAL));
  Register #(.width(32)) ID_EXTEND (.D(bit_extender_1_out), .en(1'b1), .Q(SE), .clk(Clock));  // open: clr
  // Probe on ID_EXFunct_q
  Register #(.width(32)) ID_EX_PC (.D(IF_ID_PC_q), .en(1'b1), .Q({JumpADD, PC4}), .clk(Clock));  // open: clr
  Register #(.width(10)) ID_EX_Control (
    .D(multiplexer_1_out), .en(1'b1),
    .Q({ALUOp0, ALUOp1, ID_EX_Control_q[7:6], ID_EX_MemRead, ID_EX_Control_q[4:3], ALUSrc, ID_EX_Control_q[1], RegDst}),
    .clk(Clock));  // open: clr
  // Probe on Data
  Multiplexer #(.width(5), .enable("false")) multiplexer_3 (
    .in0(ID_EX_20_16), .in1(ID_EX_15_11), .out(multiplexer_3_out), .sel(RegDst));
  Multiplexer #(.width(5), .enable("false")) multiplexer_4 (
    .in0(multiplexer_3_out), .in1({5{1'b0}}), .out(multiplexer_4_out), .sel(or_1_out));
  ROM #(.dataWidth(32)) rom_1 (.addr(divider_1_out[7:0]), .data(rom_1_data));  // open: sel
  Register_File register_file_1 (
    .WrAddr(multiplexer_2_out), .WrData(Data), .WrReg(RegWrite), .RdAddr1(INST[25:21]), .RdAddr2(_20_16),
    .RdData1(register_file_1_rddata1), .RdData2(register_file_1_rddata2), .Clock(Clock));
  Register #(.width(5)) u_EX_Mem_Inst (.D(multiplexer_4_out), .en(1'b1), .Q(EX_Mem_Inst), .clk(Clock));  // open: clr
  Multiplexer #(.width(32), .enable("false")) multiplexer_5 (
    .in0(rom_1_data), .in1({32{1'b0}}), .out(multiplexer_5_out), .sel(NOP_Decode));
  // Probe on register_file_1_rddata1
  // Probe on register_file_1_rddata2
  ALUC aluc_1 (
    .OP1(ALUOp1), .OP2(ALUOp0), .F5(ID_EXFunct_q[5]), .F4(ID_EXFunct_q[4]), .F3(ID_EXFunct_q[3]),
    .F2(ID_EXFunct_q[2]), .F1(ID_EXFunct_q[1]), .F0(ID_EXFunct_q[0]), .out3(ALUC[3]), .out2(ALUC[2]),
    .out1(ALUC[1]), .out0(ALUC[0]));
  Hazard_Unit hazard_unit_1 (
    .Branch(Branch), .IF_ID_Rt(_20_16), .IF_ID_Rs(INST[25:21]), .From_Branch(FRomBranch),
    .ID_EX_MemRead(ID_EX_MemRead), .ID_EX_Rs(RD1_2), .ID_EX_Rt(ID_EX_20_16), .PC_Write(PC_Write),
    .IF_ID_Write(IF_ID_Write), .NOP(NOP), .NOP_Decode(NOP_Decode));
  Register #(.width(32)) IF_ID (
    .D(multiplexer_5_out), .en(IF_ID_Write), .Q({INST[31:21], _20_16, _15_11, INST[10:6], Funct}), .clk(Clock));  // open: clr
  Register #(.width(32)) ID_EXRD1 (.D(register_file_1_rddata1), .en(1'b1), .Q(ID_EXRD1_q), .clk(Clock));  // open: clr
  Register #(.width(32)) ID_EXRD2 (.D(register_file_1_rddata2), .en(1'b1), .Q(ID_EXRD2_q), .clk(Clock));  // open: clr
  Register #(.width(5)) u_Mem_WB_Inst (.D(EX_Mem_Inst), .en(1'b1), .Q(Mem_WB_Inst), .clk(Clock));  // open: clr
  // Probe on EX_Mem_Inst
  // Probe on {INST[31:21], _20_16, _15_11, INST[10:6], Funct}
  Shifter #(.width(32)) shifter_1 (.in(SE), .\dist (5'b00010), .out(shifter_1_out));
  // Probe on ForA
  Multiplexer #(.select(2), .width(32), .enable("false")) multiplexer_6 (
    .in0(ID_EXRD1_q), .in1(RamData), .in2(ALURE), .out(multiplexer_6_out), .sel(ForA));  // open: in3
  Multiplexer #(.select(2), .width(32), .enable("false")) multiplexer_7 (
    .in0(ID_EXRD2_q), .in1(RamData), .in2(ALURE), .out(multiplexer_7_out), .sel(ForB));  // open: in3
  Register #(.width(32)) EX_MemRD2 (.D(multiplexer_7_out), .en(1'b1), .Q(EX_MemRD2_q), .clk(Clock));  // open: clr
  Forward_Unit forward_unit_1 (
    .RS_25_21(RD1_2), .Rt_20_16(ID_EX_20_16), .Mem_WB_RegWrite(RegWrite), .Rd_EX_Mem(EX_Mem_Inst),
    .Rd_Mem_WB(Mem_WB_Inst), .EX_Mem_RegWrite(EX_Mem_RegWrite), .ForwardA(ForA), .ForwardB(ForB));
  // Probe on nothing
  // Probe on nothing
  // Probe on nothing
  // Probe on nothing
  Register #(.width(10)) EX_Mem_Control (
    .D({2'b00, ID_EX_Control_q[7:6], ID_EX_MemRead, ID_EX_Control_q[4:3], 1'b0, ID_EX_Control_q[1], 1'b0}),
    .en(1'b1),
    .Q({EX_Mem_Control_q[9:8], Branch, MemWrite, MemRead, EX_Mem_RegWrite, EX_Mem_Control_q[3:0]}),
    .clk(Clock));  // open: clr
  Adder #(.width(32)) adder_2 (.a({JumpADD, PC4}), .b(shifter_1_out), .out(adder_2_out));  // open: cin, cout
  Register #(.width(32)) EX_Mem_RD1 (.D(multiplexer_6_out), .en(1'b1), .Q(ReadData), .clk(Clock));  // open: clr
  Multiplexer #(.width(32), .enable("false")) multiplexer_8 (
    .in0(multiplexer_7_out), .in1(SE), .out(multiplexer_8_out), .sel(ALUSrc));
  // Probe on multiplexer_8_out
  or or_1 (or_1_out, FRomBranch, JR_3_out, JAL, EX_Mem_Jump, Jl);
  // Probe on nothing
  // Probe on nothing
  // Probe on nothing
  // Probe on nothing
  Register #(.width(32)) EX_Mem_PC (.D(adder_2_out), .en(1'b1), .Q(EX_Mem_PC_q), .clk(Clock));  // open: clr
  // Probe on multiplexer_6_out
  // Probe on ForB
  Multiplexer #(.width(32), .enable("false")) multiplexer_9 (
    .in0(PCAdd1), .in1(EX_Mem_PC_q), .out(multiplexer_9_out), .sel(FRomBranch));
  ALU alu_1 (
    .ALUCtl(ALUC), .A(multiplexer_6_out), .B(multiplexer_8_out), .ALUResult(alu_1_aluresult),
    .Zero(alu_1_zero), .Shamt(SA));  // open: Overflow
  Register #(.width(1)) ID_EX_Jump (.D(Jump), .en(1'b1), .Q(ID_EX_Jump_q), .clk(Clock));  // open: clr
  JAL jal_2 (
    .Op5(INST[31]), .Op4(INST[30]), .Op3(INST[29]), .Op2(INST[28]), .Op1(INST[27]), .Op0(INST[26]),
    .JAL(jal_2_jal));
  JrFunct jrfunct_1 (
    .F5(Funct[5]), .F4(Funct[4]), .F3(Funct[3]), .F2(Funct[2]), .F1(Funct[1]), .F0(Funct[0]),
    .jr(jrfunct_1_jr));
  jrOP jrop_1 (
    .Op5(INST[31]), .Op4(INST[30]), .Op3(INST[29]), .Op2(INST[28]), .Op1(INST[27]), .Op0(INST[26]),
    .OpJr(jrop_1_opjr));
  and JR_2 (JR_2_out, Jr_F, JrOp);
  Multiplexer #(.width(32), .enable("false")) multiplexer_10 (
    .in0(multiplexer_9_out), .in1(JumpADD2), .out(multiplexer_10_out), .sel(EX_Mem_Jump));
  // Probe on alu_1_aluresult
  Register #(.width(1)) u_EX_Mem_Jump (.D(ID_EX_Jump_q), .en(1'b1), .Q(EX_Mem_Jump), .clk(Clock));  // open: clr
  Register #(.width(1)) ID_EX_JAL (.D(jal_2_jal), .en(1'b1), .Q(ID_EX_JAL_q), .clk(Clock));  // open: clr
  Register #(.width(1)) ID_EX_JrOp_F (.D(jrfunct_1_jr), .en(1'b1), .Q(ID_EX_JrOp_F_q), .clk(Clock));  // open: clr
  Register #(.width(1)) ID_EX_JrOp (.D(jrop_1_opjr), .en(1'b1), .Q(ID_EX_JrOp_q), .clk(Clock));  // open: clr
  Register #(.width(1)) Mem_WB_MemtoReg (.D(EX_Mem_Control_q[3]), .en(1'b1), .Q(MemToReg), .clk(Clock));  // open: clr
  Register #(.width(1)) Mem_WB_RegWrite (.D(EX_Mem_RegWrite), .en(1'b1), .Q(RegWrite), .clk(Clock));  // open: clr
  Multiplexer #(.width(32), .enable("false")) multiplexer_11 (
    .in0(multiplexer_10_out), .in1(ReadData), .out(PC_Back), .sel(JR_2_out));
  Register #(.width(1)) EX_Mem_Zero (.D(alu_1_zero), .en(1'b1), .Q(EX_Mem_Zero_q), .clk(Clock));  // open: clr
  Register #(.width(32)) EX_Mem_ALUR (.D(alu_1_aluresult), .en(1'b1), .Q(ALURE), .clk(Clock));  // open: clr
  and JR_3 (JR_3_out, Jr_F, JrOp);
  Register #(.width(1)) u_MEM_WB_Jump (.D(EX_Mem_Jump), .en(1'b1), .Q(Mem_WB_Jump), .clk(Clock));  // open: clr
  Register #(.width(1)) EX_Mem_JAL (.D(ID_EX_JAL_q), .en(1'b1), .Q(Jl), .clk(Clock));  // open: clr
  Register #(.width(1)) EX_Mem_JrOp_F (.D(ID_EX_JrOp_F_q), .en(1'b1), .Q(Jr_F), .clk(Clock));  // open: clr
  Register #(.width(1)) MEM_WB_JAL (.D(Jl), .en(1'b1), .Q(JAL), .clk(Clock));  // open: clr
  Register #(.width(1)) EX_Mem_JrOp (.D(ID_EX_JrOp_q), .en(1'b1), .Q(JrOp), .clk(Clock));  // open: clr
  and Branch_2 (FRomBranch, Branch, EX_Mem_Zero_q);
  // Probe on EX_MemRD2_q
  // Probe on ALURE[7:0]
  RAM #(.dataWidth(32), .bus("separate")) ram_1 (
    .addr(ALURE[7:0]), .din(EX_MemRD2_q), .data(ram_1_data), .str(MemWrite), .sel(1'b1), .clk(Clock),
    .ld(MemRead));  // open: clr
  Adder #(.width(32)) adder_3 (.a(FRom_PC), .b(32'h4), .out(adder_3_out));  // open: cin, cout
  Register #(.width(32)) Mem_WB_ALUR (.D(ALURE), .en(1'b1), .Q(Mem_WB_ALUR_q), .clk(Clock));  // open: clr
  Register #(.width(32)) Mem_WB_RD (.D(ram_1_data), .en(1'b1), .Q(Mem_WB_RD_q), .clk(Clock));  // open: clr
  Register #(.width(32)) ID_EX_JumpADD (
    .D({JumpADD, INST[25:21], _20_16, _15_11, INST[10:6], Funct, 2'b00}), .en(1'b1), .Q(ID_EX_JumpADD_q),
    .clk(Clock));  // open: clr
  Register #(.width(32)) ID_EX_Inst (.D(adder_3_out), .en(1'b1), .Q(ID_EX_Inst_q), .clk(Clock));  // open: clr
  Multiplexer #(.width(32), .enable("false")) multiplexer_12 (
    .in0(Mem_WB_ALUR_q), .in1(Mem_WB_RD_q), .out(RamData), .sel(MemToReg));
  Register #(.width(32)) EX_Mem_JumpADD (.D(ID_EX_JumpADD_q), .en(1'b1), .Q(JumpADD2), .clk(Clock));  // open: clr
  Register #(.width(32)) EX_Mem_Inst_2 (.D(ID_EX_Inst_q), .en(1'b1), .Q(EX_Mem_Inst_2_q), .clk(Clock));  // open: clr
  Register #(.width(32)) MEM_WB_Inst_2 (.D(EX_Mem_Inst_2_q), .en(1'b1), .Q(MEM_WB_Inst_2_q), .clk(Clock));  // open: clr
  Subtractor #(.width(32)) subtractor_1 (.a(MEM_WB_Inst_2_q), .b(32'h4), .out(subtractor_1_out));  // open: bin, bout
  Multiplexer #(.width(32), .enable("false")) multiplexer_13 (
    .in0(RamData), .in1(subtractor_1_out), .out(Data), .sel(Mem_WB_Jump));
  // Probe on Data
  // Probe on nothing

  // Other names for the same wires on the sheet: INST (some bits) = {_20_16, _15_11, Funct};
  //   JumpADD[27:2] = {INST[25:21], _20_16, _15_11, INST[10:6], Funct};
  //   Lazy[27:2] = {INST[25:21], _20_16, _15_11, INST[10:6], Funct}; OP[5:0] = INST[31:26]; PC4[31:28] = JumpADD;
  //   RD1[4:0] = INST[25:21]; WriteReg[4:0] = Mem_WB_Inst

  // Notes on the sheet:
  //   contents of rom_1 (hex, n*v repeats v):
  //   20010001 20020002 20030003 20040004 20050005 20060006 34270008 ac420012  434020 234824 a25022 665825
  //   c76026 c7682a 17280 27842  31500002 eb8827 8d920005
endmodule

module ALU (
  input  [3:0] ALUCtl,
  input  [31:0] A,
  input  [31:0] B,
  input  [4:0] Shamt,
  output [31:0] ALUResult,
  output Zero,
  output Overflow
);

  wire comparator_1_lt, comparator_2_lt, comparator_3_eq, comparator_4_eq, or_2_out;
  wire [31:0] ADD, AND, NOR, OR, SLL, SLT, SLTU, SRL, SUB, XOR;

  assign XOR = A ^ B;  // XOR_Gate xor_1, 32 bits wide
  Adder #(.width(32)) adder_1 (.a(A), .b(B), .out(ADD));  // open: cin, cout
  Subtractor #(.width(32)) subtractor_1 (.a(A), .b(B), .out(SUB));  // open: bin, bout
  assign AND = A & B;  // AND_Gate and_1, 32 bits wide
  assign OR = A | B;  // OR_Gate or_1, 32 bits wide
  assign NOR = ~(A | B);  // NOR_Gate nor_1, 32 bits wide
  Comparator #(.width(32)) comparator_1 (.a(A), .b(B), .lt(comparator_1_lt));  // open: gt, eq
  assign SLT = {{31{1'b0}}, comparator_1_lt};  // Bit_Extender bit_extender_1
  Shifter #(.width(32)) shifter_1 (.in(B), .\dist (Shamt), .out(SLL));
  Shifter #(.width(32), .shift("lr")) shifter_2 (.in(B), .\dist (Shamt), .out(SRL));
  Comparator #(.width(32), .mode("unsigned")) comparator_2 (.a(A), .b(B), .lt(comparator_2_lt));  // open: gt, eq
  assign SLTU = {{31{1'b0}}, comparator_2_lt};  // Bit_Extender bit_extender_2
  Multiplexer #(.select(4), .width(32), .enable("false")) multiplexer_1 (
    .in0(AND), .in1(OR), .in2(ADD), .in4(NOR), .in5(XOR), .in6(SUB), .in7(SLT), .in14(SLL), .in15(SRL),
    .out(ALUResult), .sel(ALUCtl));  // open: in3, in8, in9, in10, in11, in12, in13
  Comparator #(.width(4)) comparator_3 (.a(4'b0000), .b(ALUCtl), .eq(comparator_3_eq));  // open: gt, lt
  Comparator #(.width(4)) comparator_4 (.a(ALUCtl), .b(4'b0001), .eq(comparator_4_eq));  // open: gt, lt
  Overflow_Unit overflow_unit_1 (
    .Add(comparator_3_eq), .Sub(comparator_4_eq), .ASign(A[31]), .BSign(B[31]), .ResultSign(ALUResult[31]),
    .Overflow(Overflow));
  or or_2 (or_2_out, ALUResult[0], ALUResult[1], ALUResult[2], ALUResult[3], ALUResult[4], ALUResult[5], ALUResult[6], ALUResult[7], ALUResult[8], ALUResult[9], ALUResult[10], ALUResult[11], ALUResult[12], ALUResult[13], ALUResult[14], ALUResult[15], ALUResult[16], ALUResult[17], ALUResult[18], ALUResult[19], ALUResult[20], ALUResult[21], ALUResult[22], ALUResult[23], ALUResult[24], ALUResult[25], ALUResult[26], ALUResult[27], ALUResult[28], ALUResult[29], ALUResult[30], ALUResult[31]);
  not not_1 (Zero, or_2_out);

  // Other names for the same wires on the sheet: ASign = A[31]; ResultSign = ALUResult[31]; BSign = B[31]

  // Notes on the sheet:
  //   ALUCtl for ADD on top port
  //   ALUCtl for SUB on second port
endmodule

module Register_File (
  input  [4:0] WrAddr,
  input  [31:0] WrData,
  input  WrReg,
  input  [4:0] RdAddr1,
  input  [4:0] RdAddr2,
  input  Clock,
  output [31:0] RdData1,
  output [31:0] RdData2
);

  wire and_1_out, and_2_out, comparator_1_eq, comparator_2_eq, comparator_3_eq, comparator_4_eq, not_1_out,
       not_2_out, WrReg0, WrReg1, WrReg2, WrReg3, WrReg4, WrReg5, WrReg6, WrReg7, WrReg8, WrReg9, WrReg10,
       WrReg11, WrReg12, WrReg13, WrReg14, WrReg15, WrReg16, WrReg17, WrReg18, WrReg19, WrReg20, WrReg21,
       WrReg22, WrReg23, WrReg24, WrReg25, WrReg26, WrReg27, WrReg28, WrReg29, WrReg30, WrReg31;
  wire [31:0] multiplexer_1_out, multiplexer_2_out, RegData1, RegData2, RegData3, RegData4, RegData5,
       RegData6, RegData7, RegData8, RegData9, RegData10, RegData11, RegData12, RegData13, RegData14,
       RegData15, RegData16, RegData17, RegData18, RegData19, RegData20, RegData21, RegData22, RegData23,
       RegData24, RegData25, RegData26, RegData27, RegData28, RegData29, RegData30, RegData31;

  Demultiplexer #(.select(5), .enable("false")) demultiplexer_1 (
    .out0(WrReg0), .out1(WrReg1), .out2(WrReg2), .out3(WrReg3), .out4(WrReg4), .out5(WrReg5), .out6(WrReg6),
    .out7(WrReg7), .out8(WrReg8), .out9(WrReg9), .out10(WrReg10), .out11(WrReg11), .out12(WrReg12),
    .out13(WrReg13), .out14(WrReg14), .out15(WrReg15), .out16(WrReg16), .out17(WrReg17), .out18(WrReg18),
    .out19(WrReg19), .out20(WrReg20), .out21(WrReg21), .out22(WrReg22), .out23(WrReg23), .out24(WrReg24),
    .out25(WrReg25), .out26(WrReg26), .out27(WrReg27), .out28(WrReg28), .out29(WrReg29), .out30(WrReg30),
    .out31(WrReg31), .in(WrReg), .sel(WrAddr));
  // Probe on RegData4
  Register #(.width(32)) Reg4 (.D(WrData), .en(WrReg4), .Q(RegData4), .clk(Clock));  // open: clr
  // Probe on RegData8
  Register #(.width(32)) Reg8 (.D(WrData), .en(WrReg8), .Q(RegData8), .clk(Clock));  // open: clr
  // Probe on RegData12
  Register #(.width(32)) Reg12 (.D(WrData), .en(WrReg12), .Q(RegData12), .clk(Clock));  // open: clr
  // Probe on RegData16
  Register #(.width(32)) Reg16 (.D(WrData), .en(WrReg16), .Q(RegData16), .clk(Clock));  // open: clr
  // Probe on RegData20
  Register #(.width(32)) Reg20 (.D(WrData), .en(WrReg20), .Q(RegData20), .clk(Clock));  // open: clr
  // Probe on RegData24
  Register #(.width(32)) Reg24 (.D(WrData), .en(WrReg24), .Q(RegData24), .clk(Clock));  // open: clr
  // Probe on RegData28
  Register #(.width(32)) Reg28 (.D(WrData), .en(WrReg28), .Q(RegData28), .clk(Clock));  // open: clr
  Register #(.width(32)) Reg1 (.D(WrData), .en(WrReg1), .Q(RegData1), .clk(Clock));  // open: clr
  Register #(.width(32)) Reg5 (.D(WrData), .en(WrReg5), .Q(RegData5), .clk(Clock));  // open: clr
  Register #(.width(32)) Reg9 (.D(WrData), .en(WrReg9), .Q(RegData9), .clk(Clock));  // open: clr
  Register #(.width(32)) Reg13 (.D(WrData), .en(WrReg13), .Q(RegData13), .clk(Clock));  // open: clr
  Register #(.width(32)) Reg17 (.D(WrData), .en(WrReg17), .Q(RegData17), .clk(Clock));  // open: clr
  Register #(.width(32)) Reg21 (.D(WrData), .en(WrReg21), .Q(RegData21), .clk(Clock));  // open: clr
  Register #(.width(32)) Reg25 (.D(WrData), .en(WrReg25), .Q(RegData25), .clk(Clock));  // open: clr
  Register #(.width(32)) Reg29 (.D(WrData), .en(WrReg29), .Q(RegData29), .clk(Clock));  // open: clr
  // Probe on RegData1
  // Probe on RegData5
  // Probe on RegData9
  // Probe on RegData13
  // Probe on RegData17
  // Probe on RegData21
  // Probe on RegData25
  // Probe on RegData29
  // Probe on RegData2
  Register #(.width(32)) Reg2 (.D(WrData), .en(WrReg2), .Q(RegData2), .clk(Clock));  // open: clr
  // Probe on RegData6
  Register #(.width(32)) Reg6 (.D(WrData), .en(WrReg6), .Q(RegData6), .clk(Clock));  // open: clr
  // Probe on RegData10
  Register #(.width(32)) Reg10 (.D(WrData), .en(WrReg10), .Q(RegData10), .clk(Clock));  // open: clr
  // Probe on RegData14
  Register #(.width(32)) Reg14 (.D(WrData), .en(WrReg14), .Q(RegData14), .clk(Clock));  // open: clr
  // Probe on RegData18
  Register #(.width(32)) Reg18 (.D(WrData), .en(WrReg18), .Q(RegData18), .clk(Clock));  // open: clr
  // Probe on RegData22
  Register #(.width(32)) Reg22 (.D(WrData), .en(WrReg22), .Q(RegData22), .clk(Clock));  // open: clr
  // Probe on RegData26
  Register #(.width(32)) Reg26 (.D(WrData), .en(WrReg26), .Q(RegData26), .clk(Clock));  // open: clr
  // Probe on RegData30
  Register #(.width(32)) Reg30 (.D(WrData), .en(WrReg30), .Q(RegData30), .clk(Clock));  // open: clr
  // Probe on RegData3
  Register #(.width(32)) Reg3 (.D(WrData), .en(WrReg3), .Q(RegData3), .clk(Clock));  // open: clr
  // Probe on RegData7
  Register #(.width(32)) Reg7 (.D(WrData), .en(WrReg7), .Q(RegData7), .clk(Clock));  // open: clr
  // Probe on RegData11
  Register #(.width(32)) Reg11 (.D(WrData), .en(WrReg11), .Q(RegData11), .clk(Clock));  // open: clr
  // Probe on RegData15
  Register #(.width(32)) Reg15 (.D(WrData), .en(WrReg15), .Q(RegData15), .clk(Clock));  // open: clr
  // Probe on RegData19
  Register #(.width(32)) Reg19 (.D(WrData), .en(WrReg19), .Q(RegData19), .clk(Clock));  // open: clr
  // Probe on RegData23
  Register #(.width(32)) Reg23 (.D(WrData), .en(WrReg23), .Q(RegData23), .clk(Clock));  // open: clr
  // Probe on RegData27
  Register #(.width(32)) Reg27 (.D(WrData), .en(WrReg27), .Q(RegData27), .clk(Clock));  // open: clr
  // Probe on RegData31
  Register #(.width(32)) Reg31 (.D(WrData), .en(WrReg31), .Q(RegData31), .clk(Clock));  // open: clr
  Multiplexer #(.select(5), .width(32), .enable("false")) multiplexer_1 (
    .in0({32{1'b0}}), .in1(RegData1), .in2(RegData2), .in3(RegData3), .in4(RegData4), .in5(RegData5),
    .in6(RegData6), .in7(RegData7), .in8(RegData8), .in9(RegData9), .in10(RegData10), .in11(RegData11),
    .in12(RegData12), .in13(RegData13), .in14(RegData14), .in15(RegData15), .in16(RegData16),
    .in17(RegData17), .in18(RegData18), .in19(RegData19), .in20(RegData20), .in21(RegData21),
    .in22(RegData22), .in23(RegData23), .in24(RegData24), .in25(RegData25), .in26(RegData26),
    .in27(RegData27), .in28(RegData28), .in29(RegData29), .in30(RegData30), .in31(RegData31),
    .out(multiplexer_1_out), .sel(RdAddr1));
  Multiplexer #(.select(5), .width(32), .enable("false")) multiplexer_2 (
    .in0({32{1'b0}}), .in1(RegData1), .in2(RegData2), .in3(RegData3), .in4(RegData4), .in5(RegData5),
    .in6(RegData6), .in7(RegData7), .in8(RegData8), .in9(RegData9), .in10(RegData10), .in11(RegData11),
    .in12(RegData12), .in13(RegData13), .in14(RegData14), .in15(RegData15), .in16(RegData16),
    .in17(RegData17), .in18(RegData18), .in19(RegData19), .in20(RegData20), .in21(RegData21),
    .in22(RegData22), .in23(RegData23), .in24(RegData24), .in25(RegData25), .in26(RegData26),
    .in27(RegData27), .in28(RegData28), .in29(RegData29), .in30(RegData30), .in31(RegData31),
    .out(multiplexer_2_out), .sel(RdAddr2));
  Multiplexer #(.width(32), .enable("false")) multiplexer_3 (
    .in0(multiplexer_1_out), .in1(WrData), .out(RdData1), .sel(and_1_out));
  Comparator #(.width(5), .mode("unsigned")) comparator_1 (
    .a(WrAddr), .b(RdAddr2), .eq(comparator_1_eq));  // open: gt, lt
  Multiplexer #(.width(32), .enable("false")) multiplexer_4 (
    .in0(multiplexer_2_out), .in1(WrData), .out(RdData2), .sel(and_2_out));
  Comparator #(.width(5), .mode("unsigned")) comparator_2 (
    .a(WrAddr), .b(RdAddr1), .eq(comparator_2_eq));  // open: gt, lt
  and and_1 (and_1_out, comparator_2_eq, WrReg, not_1_out);
  and and_2 (and_2_out, comparator_1_eq, WrReg, not_2_out);
  Comparator #(.width(5), .mode("unsigned")) comparator_3 (
    .a(WrAddr), .b({5{1'b0}}), .eq(comparator_3_eq));  // open: gt, lt
  not not_1 (not_1_out, comparator_3_eq);
  Comparator #(.width(5), .mode("unsigned")) comparator_4 (
    .a(WrAddr), .b({5{1'b0}}), .eq(comparator_4_eq));  // open: gt, lt
  not not_2 (not_2_out, comparator_4_eq);
endmodule

module Overflow_Unit (
  input  Add,
  input  Sub,
  input  ASign,
  input  BSign,
  input  ResultSign,
  output Overflow
);

  wire and_1_out, and_2_out, or_1_out, xnor_1_out, xor_1_out, xor_2_out;

  xnor xnor_1 (xnor_1_out, ASign, BSign);
  xor xor_1 (xor_1_out, ASign, BSign);
  and and_1 (and_1_out, xnor_1_out, Add);
  and and_2 (and_2_out, xor_1_out, Sub);
  or or_1 (or_1_out, and_1_out, and_2_out);
  xor xor_2 (xor_2_out, ResultSign, ASign);
  and and_3 (Overflow, or_1_out, xor_2_out);

  // Notes on the sheet:
  //   Overflow occurs when doing addition and sign(A) == sign(B) && sign(result) != sign(A)
  //   Or
  //   Overflow occurs when doing subtraction and sign(A) != sign(B) && sign(result) != sign(A)
endmodule

module ALUC (
  input  OP1,
  input  OP2,
  input  F5,
  input  F4,
  input  F3,
  input  F2,
  input  F1,
  input  F0,
  output out3,
  output out2,
  output out1,
  output out0
);

  wire and_1_out, and_2_out, and_3_out, and_4_out, and_5_out, and_6_out, and_7_out, and_8_out, and_9_out,
       and_10_out, and_11_out, and_12_out, and_13_out, and_14_out, and_15_out, and_16_out, and_17_out,
       and_18_out, and_19_out, and_20_out, and_21_out, and_22_out, and_23_out, and_24_out, and_25_out,
       and_26_out, and_27_out, and_28_out, and_29_out, and_30_out, and_31_out, and_32_out, and_33_out,
       and_34_out, and_35_out, and_36_out, and_37_out, and_38_out, and_39_out, and_40_out, and_41_out,
       and_42_out, and_43_out, and_44_out, and_45_out, and_46_out, and_47_out, and_48_out, and_49_out,
       not_1_out, not_2_out, not_3_out, not_4_out, not_5_out, not_6_out, not_7_out, not_8_out, not_9_out,
       not_10_out, not_11_out, not_12_out, not_13_out, not_14_out, not_15_out, not_16_out, not_17_out,
       not_18_out, not_19_out, not_20_out, not_21_out, not_22_out, not_23_out, not_24_out, not_25_out,
       not_26_out, not_27_out, not_28_out, not_29_out, not_30_out, not_31_out, not_32_out, not_33_out,
       not_34_out, not_35_out, not_36_out, not_37_out, not_38_out, not_39_out, not_40_out, not_41_out,
       not_42_out, not_43_out, not_44_out, not_45_out, not_46_out, not_47_out, not_48_out, not_49_out,
       not_50_out, not_51_out, not_52_out, not_53_out, not_54_out, not_55_out, not_56_out, not_57_out,
       not_58_out, not_59_out, not_60_out, not_61_out, not_62_out, not_63_out, not_64_out, not_65_out,
       not_66_out, not_67_out, not_68_out, not_69_out, not_70_out, not_71_out, not_72_out, not_73_out,
       not_74_out, not_75_out, not_76_out, not_77_out, not_78_out, not_79_out, not_80_out, not_81_out,
       not_82_out, not_83_out, not_84_out, not_85_out, not_86_out, not_87_out, not_88_out, not_89_out,
       not_90_out, not_91_out, not_92_out, not_93_out, not_94_out, not_95_out, not_96_out, not_97_out,
       not_98_out, not_99_out, not_100_out, not_101_out, not_102_out, not_103_out, not_104_out, not_105_out,
       not_106_out;

  not not_1 (not_1_out, OP2);
  not not_2 (not_2_out, F5);
  not not_3 (not_3_out, F4);
  not not_4 (not_4_out, F3);
  not not_5 (not_5_out, F2);
  not not_6 (not_6_out, F0);
  not not_7 (not_7_out, OP2);
  not not_8 (not_8_out, F5);
  not not_9 (not_9_out, F4);
  not not_10 (not_10_out, F2);
  not not_11 (not_11_out, F1);
  not not_12 (not_12_out, F0);
  not not_13 (not_13_out, OP2);
  not not_14 (not_14_out, F5);
  not not_15 (not_15_out, F3);
  not not_16 (not_16_out, F2);
  not not_17 (not_17_out, F1);
  not not_18 (not_18_out, F0);
  not not_19 (not_19_out, OP1);
  not not_20 (not_20_out, F5);
  not not_21 (not_21_out, F4);
  not not_22 (not_22_out, F1);
  not not_23 (not_23_out, OP1);
  not not_24 (not_24_out, F2);
  not not_25 (not_25_out, OP1);
  not not_26 (not_26_out, F5);
  not not_27 (not_27_out, F4);
  not not_28 (not_28_out, OP1);
  not not_29 (not_29_out, F5);
  not not_30 (not_30_out, OP1);
  not not_31 (not_31_out, F1);
  not not_32 (not_32_out, F0);
  not not_33 (not_33_out, F3);
  not not_34 (not_34_out, OP1);
  not not_35 (not_35_out, F3);
  not not_36 (not_36_out, OP2);
  not not_37 (not_37_out, F5);
  not not_38 (not_38_out, F4);
  not not_39 (not_39_out, F2);
  not not_40 (not_40_out, F0);
  not not_41 (not_41_out, OP2);
  not not_42 (not_42_out, F5);
  not not_43 (not_43_out, F3);
  not not_44 (not_44_out, F2);
  not not_45 (not_45_out, F0);
  not not_46 (not_46_out, F0);
  not not_47 (not_47_out, F5);
  not not_48 (not_48_out, F5);
  not not_49 (not_49_out, F2);
  not not_50 (not_50_out, F4);
  not not_51 (not_51_out, F3);
  not not_52 (not_52_out, OP1);
  not not_53 (not_53_out, OP2);
  not not_54 (not_54_out, F3);
  not not_55 (not_55_out, OP2);
  not not_56 (not_56_out, F3);
  not not_57 (not_57_out, F2);
  not not_58 (not_58_out, F4);
  not not_59 (not_59_out, F3);
  not not_60 (not_60_out, F2);
  not not_61 (not_61_out, F1);
  not not_62 (not_62_out, F0);
  not not_63 (not_63_out, OP1);
  not not_64 (not_64_out, F5);
  not not_65 (not_65_out, OP1);
  not not_66 (not_66_out, F5);
  not not_67 (not_67_out, OP1);
  not not_68 (not_68_out, F4);
  not not_69 (not_69_out, OP1);
  not not_70 (not_70_out, F1);
  not not_71 (not_71_out, OP1);
  not not_72 (not_72_out, F0);
  not not_73 (not_73_out, F2);
  not not_74 (not_74_out, F2);
  not not_75 (not_75_out, F2);
  not not_76 (not_76_out, OP1);
  not not_77 (not_77_out, F3);
  not not_78 (not_78_out, F2);
  not not_79 (not_79_out, F2);
  not not_80 (not_80_out, OP1);
  not not_81 (not_81_out, OP2);
  not not_82 (not_82_out, F4);
  not not_83 (not_83_out, F3);
  not not_84 (not_84_out, F1);
  not not_85 (not_85_out, OP1);
  not not_86 (not_86_out, F4);
  not not_87 (not_87_out, F3);
  not not_88 (not_88_out, F0);
  not not_89 (not_89_out, F4);
  not not_90 (not_90_out, F2);
  not not_91 (not_91_out, F0);
  not not_92 (not_92_out, F1);
  not not_93 (not_93_out, OP2);
  not not_94 (not_94_out, F5);
  not not_95 (not_95_out, F4);
  not not_96 (not_96_out, F2);
  not not_97 (not_97_out, F0);
  not not_98 (not_98_out, F5);
  not not_99 (not_99_out, F4);
  not not_100 (not_100_out, F2);
  not not_101 (not_101_out, F0);
  not not_102 (not_102_out, F3);
  not not_103 (not_103_out, F2);
  not not_104 (not_104_out, OP2);
  not not_105 (not_105_out, F4);
  not not_106 (not_106_out, F0);
  and and_1 (and_1_out, OP1, not_1_out, not_2_out, not_3_out, not_4_out, not_5_out, not_6_out);
  and and_2 (and_2_out, OP1, not_7_out, not_8_out, not_9_out, not_10_out, not_11_out, not_12_out);
  and and_3 (and_3_out, OP1, not_13_out, not_14_out, not_15_out, not_16_out, not_17_out, not_18_out);
  and and_4 (and_4_out, not_19_out, OP2, not_20_out, not_21_out, not_22_out);
  and and_5 (and_5_out, not_23_out, OP2, not_24_out, F0);
  and and_6 (and_6_out, not_25_out, OP2, not_26_out, F2);
  and and_7 (and_7_out, OP2, not_27_out, F2, F1);
  and and_8 (and_8_out, not_28_out, OP2, not_29_out, F3);
  and and_9 (and_9_out, not_30_out, OP2, F3, not_31_out);
  and and_10 (and_10_out, OP2, F4, F1, not_32_out);
  and and_11 (and_11_out, OP2, F5, not_33_out, F1);
  and and_12 (and_12_out, not_34_out, OP2, F5, F4, not_35_out);
  and and_13 (and_13_out, OP1, not_36_out, not_37_out, not_38_out, not_39_out, not_40_out);
  and and_14 (and_14_out, OP1, not_41_out, not_42_out, not_43_out, not_44_out, not_45_out);
  and and_15 (and_15_out, OP1, F1, not_46_out);
  and and_16 (and_16_out, OP1, not_47_out, F2, F1);
  and and_17 (and_17_out, OP1, not_48_out, F3, F1);
  and and_18 (and_18_out, OP1, F4, not_49_out, F1);
  and and_19 (and_19_out, OP1, F5, not_50_out, F1);
  and and_20 (and_20_out, OP1, F5, not_51_out, F1);
  and and_21 (and_21_out, OP1, OP2, F1);
  and and_22 (and_22_out, not_52_out, not_53_out, not_54_out);
  and and_23 (and_23_out, not_55_out, not_56_out, not_57_out);
  and and_24 (and_24_out, not_58_out, not_59_out, not_60_out, not_61_out, not_62_out);
  and and_25 (and_25_out, not_63_out, not_64_out, F0);
  and and_26 (and_26_out, not_65_out, not_66_out, F2);
  and and_27 (and_27_out, not_67_out, not_68_out, F3);
  and and_28 (and_28_out, not_69_out, F3, not_70_out);
  and and_29 (and_29_out, not_71_out, F3, not_72_out);
  and and_30 (and_30_out, F3, not_73_out, F0);
  and and_31 (and_31_out, F4, not_74_out, F1);
  and and_32 (and_32_out, F5, not_75_out);
  and and_33 (and_33_out, not_76_out, F5, F4, not_77_out);
  and and_34 (and_34_out, OP1, not_78_out, F1);
  and and_35 (and_35_out, OP1, F4, not_79_out);
  and and_36 (and_36_out, not_80_out, not_81_out, F5, F4, F3, F2, F1, F0);
  and and_37 (and_37_out, OP2, F5, not_82_out, not_83_out, F2, not_84_out, F0);
  and and_38 (and_38_out, not_85_out, OP2, F5, not_86_out, not_87_out, F2, F1, not_88_out);
  and and_39 (and_39_out, OP2, F5, not_89_out, F3, not_90_out, F1, not_91_out);
  and and_40 (and_40_out, OP1, not_92_out, F0);
  and and_41 (and_41_out, OP1, not_93_out, not_94_out, not_95_out, not_96_out, F1, not_97_out);
  and and_42 (and_42_out, OP1, not_98_out, F2, F0);
  and and_43 (and_43_out, OP1, not_99_out, F3);
  and and_44 (and_44_out, OP1, F3, not_100_out);
  and and_45 (and_45_out, OP1, F3, not_101_out);
  and and_46 (and_46_out, OP1, F4, not_102_out, F0);
  and and_47 (and_47_out, OP1, F5, not_103_out, F0);
  and and_48 (and_48_out, OP1, not_104_out, F5, not_105_out, F2, F1, not_106_out);
  and and_49 (and_49_out, OP1, OP2, F0);
  or or_1 (out3, and_1_out, and_2_out, and_3_out);
  or or_2 (out1, and_22_out, and_23_out, and_24_out, and_25_out, and_26_out, and_27_out, and_28_out, and_29_out, and_30_out, and_31_out, and_32_out, and_33_out, and_34_out, and_35_out);
  or or_3 (out0, and_36_out, and_37_out, and_38_out, and_39_out, and_40_out, and_41_out, and_42_out, and_43_out, and_44_out, and_45_out, and_46_out, and_47_out, and_48_out, and_49_out);
  or or_4 (out2, and_4_out, and_5_out, and_6_out, and_7_out, and_8_out, and_9_out, and_10_out, and_11_out, and_12_out, and_13_out, and_14_out, and_15_out, and_16_out, and_17_out, and_18_out, and_19_out, and_20_out, and_21_out);
endmodule

module Control (
  input  Op5,
  input  Op4,
  input  Op3,
  input  Op2,
  input  Op1,
  input  Op0,
  output RegDst,
  output Jump,
  output ALUSrc,
  output MemtoReg,
  output RegWrite,
  output MemRead,
  output MemWrite,
  output Branch,
  output ALUOp1,
  output ALUOp0
);

  wire and_1_out, and_2_out, and_3_out, and_4_out, and_5_out, and_7_out, and_8_out, and_9_out, and_10_out,
       and_11_out, and_12_out, and_13_out, and_14_out, and_15_out, and_16_out, and_17_out, and_18_out,
       and_19_out, and_20_out, and_21_out, and_22_out, and_23_out, and_24_out, and_25_out, and_26_out,
       and_27_out, and_28_out, and_29_out, and_30_out, and_31_out, and_32_out, not_1_out, not_2_out,
       not_3_out, not_4_out, not_5_out, not_6_out, not_7_out, not_8_out, not_9_out, not_10_out, not_11_out,
       not_12_out, not_13_out, not_14_out, not_15_out, not_16_out, not_17_out, not_18_out, not_19_out,
       not_20_out, not_21_out, not_22_out, not_23_out, not_24_out, not_25_out, not_26_out, not_27_out,
       not_28_out, not_29_out, not_30_out, not_31_out, not_32_out, not_33_out, not_34_out, not_35_out,
       not_36_out, not_37_out, not_38_out, not_39_out, not_40_out, not_41_out, not_42_out, not_43_out,
       not_44_out, not_45_out, not_46_out, not_47_out, not_48_out, not_49_out, not_50_out, not_51_out,
       not_52_out, not_53_out, not_54_out, not_55_out, not_56_out, not_57_out, not_58_out;

  not not_1 (not_1_out, Op5);
  not not_2 (not_2_out, Op4);
  not not_3 (not_3_out, Op3);
  not not_4 (not_4_out, Op2);
  not not_5 (not_5_out, Op3);
  not not_6 (not_6_out, Op1);
  not not_7 (not_7_out, Op2);
  not not_8 (not_8_out, Op1);
  not not_9 (not_9_out, Op1);
  not not_10 (not_10_out, Op1);
  not not_11 (not_11_out, Op5);
  not not_12 (not_12_out, Op4);
  not not_13 (not_13_out, Op3);
  not not_14 (not_14_out, Op2);
  not not_15 (not_15_out, Op5);
  not not_16 (not_16_out, Op4);
  not not_17 (not_17_out, Op0);
  not not_18 (not_18_out, Op5);
  not not_19 (not_19_out, Op4);
  not not_20 (not_20_out, Op5);
  not not_21 (not_21_out, Op4);
  not not_22 (not_22_out, Op2);
  not not_23 (not_23_out, Op1);
  not not_24 (not_24_out, Op0);
  not not_25 (not_25_out, Op3);
  not not_26 (not_26_out, Op2);
  not not_27 (not_27_out, Op5);
  not not_28 (not_28_out, Op4);
  not not_29 (not_29_out, Op1);
  not not_30 (not_30_out, Op3);
  not not_31 (not_31_out, Op2);
  not not_32 (not_32_out, Op3);
  not not_33 (not_33_out, Op2);
  not not_34 (not_34_out, Op3);
  not not_35 (not_35_out, Op3);
  not not_36 (not_36_out, Op3);
  not not_37 (not_37_out, Op2);
  not not_38 (not_38_out, Op0);
  not not_39 (not_39_out, Op5);
  not not_40 (not_40_out, Op4);
  not not_41 (not_41_out, Op3);
  not not_42 (not_42_out, Op0);
  not not_43 (not_43_out, Op3);
  not not_44 (not_44_out, Op0);
  not not_45 (not_45_out, Op5);
  not not_46 (not_46_out, Op4);
  not not_47 (not_47_out, Op3);
  not not_48 (not_48_out, Op2);
  not not_49 (not_49_out, Op5);
  not not_50 (not_50_out, Op4);
  not not_51 (not_51_out, Op1);
  not not_52 (not_52_out, Op2);
  not not_53 (not_53_out, Op1);
  not not_54 (not_54_out, Op2);
  not not_55 (not_55_out, Op1);
  not not_56 (not_56_out, Op5);
  not not_57 (not_57_out, Op4);
  not not_58 (not_58_out, Op3);
  and and_1 (and_1_out, not_1_out, not_2_out, not_3_out, not_4_out);
  and and_2 (and_2_out, not_5_out, not_6_out);
  and and_3 (and_3_out, not_7_out, not_8_out, Op0);
  and and_4 (and_4_out, Op4, not_9_out);
  and and_5 (and_5_out, Op5, not_10_out);
  and and_6 (Jump, not_11_out, not_12_out, not_13_out, not_14_out, Op1);
  and and_7 (and_7_out, not_15_out, not_16_out, Op3, not_17_out);
  and and_8 (and_8_out, not_18_out, not_19_out, Op3, Op2);
  and and_9 (and_9_out, not_20_out, not_21_out, not_22_out, not_23_out, not_24_out);
  and and_10 (and_10_out, not_25_out, not_26_out, Op0);
  and and_11 (and_11_out, not_27_out, not_28_out, Op3, Op2, not_29_out);
  and and_12 (and_12_out, Op4, not_30_out, not_31_out);
  and and_13 (and_13_out, Op5, not_32_out, not_33_out);
  and and_14 (and_14_out, not_34_out, Op2, Op1);
  and and_15 (and_15_out, Op4, not_35_out, Op1);
  and and_16 (and_16_out, Op5, not_36_out, Op1);
  and and_17 (and_17_out, Op3, not_37_out, Op0);
  and and_18 (and_18_out, Op3, Op1);
  and and_19 (and_19_out, Op3, Op2, not_38_out);
  and and_20 (and_20_out, Op4, Op3);
  and and_21 (and_21_out, Op5, Op3);
  and and_22 (and_22_out, not_39_out, not_40_out, not_41_out, Op1, not_42_out);
  and and_23 (and_23_out, not_43_out, Op2);
  and and_24 (and_24_out, Op2, not_44_out);
  and and_25 (and_25_out, Op2, Op1);
  and and_26 (and_26_out, Op4, Op2);
  and and_27 (and_27_out, Op5, Op2);
  and and_28 (and_28_out, not_45_out, not_46_out, not_47_out, not_48_out);
  and and_29 (and_29_out, not_49_out, not_50_out, Op3, not_51_out, Op0);
  and and_30 (and_30_out, Op4, not_52_out, not_53_out);
  and and_31 (and_31_out, Op5, not_54_out, not_55_out);
  and and_32 (and_32_out, not_56_out, not_57_out, not_58_out, Op1);
  or or_1 (RegDst, and_1_out, and_2_out, and_3_out, and_4_out, and_5_out);
  or or_2 (ALUSrc, Op1, and_7_out, and_8_out);
  or or_3 (RegWrite, and_9_out, and_10_out, and_11_out, and_12_out, and_13_out);
  or or_4 (MemRead, and_14_out, and_15_out, and_16_out);
  or or_5 (MemWrite, and_17_out, and_18_out, and_19_out, and_20_out, and_21_out);
  or or_6 (Branch, and_22_out, and_23_out, and_24_out, and_25_out, and_26_out, and_27_out);
  or or_7 (ALUOp1, and_28_out, and_29_out, and_30_out, and_31_out);
  or or_8 (ALUOp0, and_32_out, Op2);

  assign MemtoReg = Op1;
endmodule

module Forward_Unit (
  input  [4:0] Rd_EX_Mem,
  input  Mem_WB_RegWrite,
  input  EX_Mem_RegWrite,
  input  [4:0] RS_25_21,
  input  [4:0] Rt_20_16,
  input  [4:0] Rd_Mem_WB,
  output [1:0] ForwardA,
  output [1:0] ForwardB
);

  wire _01A_out, _01B_out, _10A_out, _10B_out, comparator_1_eq, comparator_2_eq, comparator_3_eq,
       comparator_4_eq, comparator_5_eq, comparator_6_eq, not_1_out, not_2_out, not_3_out, not_4_out;
  wire [1:0] multiplexer_1_out, multiplexer_2_out, multiplexer_3_out, multiplexer_4_out;

  Comparator #(.width(5)) comparator_1 (.a(Rd_EX_Mem), .b({5{1'b0}}), .eq(comparator_1_eq));  // open: gt, lt
  not not_1 (not_1_out, comparator_1_eq);
  Comparator #(.width(5)) comparator_2 (.a(Rd_Mem_WB), .b({5{1'b0}}), .eq(comparator_2_eq));  // open: gt, lt
  not not_2 (not_2_out, comparator_2_eq);
  Comparator #(.width(5)) comparator_3 (.a(Rd_EX_Mem), .b(RS_25_21), .eq(comparator_3_eq));  // open: gt, lt
  Comparator #(.width(5)) comparator_4 (.a(Rd_EX_Mem), .b(Rt_20_16), .eq(comparator_4_eq));  // open: gt, lt
  Comparator #(.width(5)) comparator_5 (.a(Rd_Mem_WB), .b(RS_25_21), .eq(comparator_5_eq));  // open: gt, lt
  Comparator #(.width(5)) comparator_6 (.a(Rd_Mem_WB), .b(Rt_20_16), .eq(comparator_6_eq));  // open: gt, lt
  and _10A (_10A_out, not_1_out, comparator_3_eq, EX_Mem_RegWrite);
  and _10B (_10B_out, not_1_out, comparator_4_eq, EX_Mem_RegWrite);
  not not_3 (not_3_out, _10B_out);
  not not_4 (not_4_out, _10A_out);
  Multiplexer #(.width(2), .enable("false")) multiplexer_1 (
    .in0(2'b00), .in1(2'b10), .out(multiplexer_1_out), .sel(_10A_out));
  Multiplexer #(.width(2), .enable("false")) multiplexer_2 (
    .in0(2'b00), .in1(2'b10), .out(multiplexer_2_out), .sel(_10B_out));
  and _01A (_01A_out, not_2_out, comparator_5_eq, Mem_WB_RegWrite, not_4_out);
  and _01B (_01B_out, not_2_out, not_3_out, Mem_WB_RegWrite, comparator_6_eq);
  Multiplexer #(.width(2), .enable("false")) multiplexer_3 (
    .in0(2'b00), .in1(2'b01), .out(multiplexer_3_out), .sel(_01A_out));
  Multiplexer #(.width(2), .enable("false")) multiplexer_4 (
    .in0(2'b00), .in1(2'b01), .out(multiplexer_4_out), .sel(_01B_out));
  ExactlyOne A[1:0] (.out(ForwardA), .in0(2'b00), .in1(multiplexer_1_out), .in2(multiplexer_3_out));
  ExactlyOne B[1:0] (.out(ForwardB), .in0(2'b00), .in1(multiplexer_2_out), .in2(multiplexer_4_out));
endmodule

module Hazard_Unit (
  input  [4:0] ID_EX_Rs,
  input  [4:0] IF_ID_Rt,
  input  [4:0] IF_ID_Rs,
  input  ID_EX_MemRead,
  input  [4:0] ID_EX_Rt,
  input  From_Branch,
  input  Branch,
  output PC_Write,
  output IF_ID_Write,
  output NOP,
  output NOP_Decode
);

  wire and_1_out, comparator_1_eq, comparator_2_eq, comparator_3_eq, multiplexer_1_out, not_1_out, not_2_out,
       or_1_out;

  Comparator #(.width(5)) comparator_1 (.a(ID_EX_Rt), .b(IF_ID_Rs), .eq(comparator_1_eq));  // open: gt, lt
  Comparator #(.width(5)) comparator_2 (.a(ID_EX_Rt), .b(IF_ID_Rt), .eq(comparator_2_eq));  // open: gt, lt
  Comparator #(.width(5)) comparator_3 (.a(ID_EX_Rt), .b({5{1'b0}}), .eq(comparator_3_eq));  // open: gt, lt
  not not_1 (not_1_out, comparator_3_eq);
  and D_E_NOP (NOP_Decode, From_Branch, Branch);
  or or_1 (or_1_out, comparator_1_eq, comparator_2_eq);
  and and_1 (and_1_out, ID_EX_MemRead, not_1_out, or_1_out);
  Multiplexer #(.enable("false")) multiplexer_1 (.in0(1'b1), .in1(1'b0), .out(multiplexer_1_out), .sel(and_1_out));
  buf or_2 (IF_ID_Write, multiplexer_1_out);  // OR_Gate
  not not_2 (not_2_out, IF_ID_Write);
  or or_3 (NOP, not_2_out, NOP_Decode);

  assign PC_Write = IF_ID_Write;
endmodule

module jrOP (
  input  Op5,
  input  Op4,
  input  Op3,
  input  Op2,
  input  Op1,
  input  Op0,
  output OpJr
);

  wire not_1_out, not_2_out, not_3_out, not_4_out, not_5_out, not_6_out;

  not not_1 (not_1_out, Op5);
  not not_2 (not_2_out, Op4);
  not not_3 (not_3_out, Op3);
  not not_4 (not_4_out, Op2);
  not not_5 (not_5_out, Op1);
  not not_6 (not_6_out, Op0);
  and and_1 (OpJr, not_1_out, not_2_out, not_3_out, not_4_out, not_5_out, not_6_out);
endmodule

module JrFunct (
  input  F5,
  input  F4,
  input  F3,
  input  F2,
  input  F1,
  input  F0,
  output jr
);

  wire not_1_out, not_2_out, not_3_out, not_4_out, not_5_out;

  not not_1 (not_1_out, F5);
  not not_2 (not_2_out, F4);
  not not_3 (not_3_out, F2);
  not not_4 (not_4_out, F1);
  not not_5 (not_5_out, F0);
  and and_1 (jr, not_1_out, not_2_out, F3, not_3_out, not_4_out, not_5_out);
endmodule

module JAL (
  input  Op5,
  input  Op4,
  input  Op3,
  input  Op2,
  input  Op1,
  input  Op0,
  output JAL
);

  wire not_1_out, not_2_out, not_3_out, not_4_out;

  not not_1 (not_1_out, Op5);
  not not_2 (not_2_out, Op4);
  not not_3 (not_3_out, Op3);
  not not_4 (not_4_out, Op2);
  and and_1 (JAL, not_1_out, not_2_out, not_3_out, not_4_out, Op1, Op0);
endmodule
